// Logisim project My3.circ as structural Verilog: 14 circuits, main circuit 四位二进制可逆计数器置9
module \四位二进制可逆计数器置9  (
  input  CPU,
  input  CPD,
  input  \置9 ,
  input  CLR,
  output QA,
  output QB,
  output QC,
  output QD
);

  wire and_1_out, and_2_out, and_3_out, and_4_out, and_5_out, and_6_out, d_ff_1_qn, d_ff_2_qn, d_ff_3_qn,
       not_1_out, not_2_out, not_3_out, not_4_out, or_1_out, or_2_out, or_3_out, or_4_out, or_5_out, or_6_out;

  and and_1 (and_1_out, CPD, d_ff_1_qn);
  and and_2 (and_2_out, QA, CPU);
  and and_3 (and_3_out, CPD, d_ff_1_qn, d_ff_2_qn);
  and and_4 (and_4_out, QA, QB, CPU);
  and and_5 (and_5_out, CPD, d_ff_1_qn, d_ff_3_qn, d_ff_2_qn);
  and and_6 (and_6_out, QA, QB, QC, CPU);
  or or_1 (or_1_out, and_1_out, and_2_out);
  or or_2 (or_2_out, and_3_out, and_4_out);
  or or_3 (or_3_out, and_5_out, and_6_out);
  or or_4 (or_4_out, CPU, CPD);
  not not_1 (not_1_out, QA);
  not not_2 (not_2_out, QB);
  not not_3 (not_3_out, QC);
  not not_4 (not_4_out, QD);
  D_Flip_Flop #(.trigger("falling")) d_ff_1 (
    .clk(or_4_out), .D(not_1_out), .Q(QA), .Qn(d_ff_1_qn), .preset(\置9 ), .en(1'b1), .reset(CLR));
  D_Flip_Flop #(.trigger("falling")) d_ff_2 (
    .clk(or_1_out), .D(not_2_out), .Q(QB), .Qn(d_ff_2_qn), .preset(1'b0), .en(1'b1), .reset(or_5_out));
  or or_5 (or_5_out, CLR, \置9 );
  D_Flip_Flop #(.trigger("falling")) d_ff_3 (
    .clk(or_2_out), .D(not_3_out), .Q(QC), .Qn(d_ff_3_qn), .preset(1'b0), .en(1'b1), .reset(or_6_out));
  or or_6 (or_6_out, CLR, \置9 );
  D_Flip_Flop #(.trigger("falling")) d_ff_4 (
    .clk(or_3_out), .D(not_4_out), .Q(QD), .preset(\置9 ), .en(1'b1), .reset(CLR));  // open: Qn
endmodule

module \带校准功能的六十进制计数器  (
  input  in_1,
  input  in_2,
  input  in_3,
  input  in_4,
  output out_5,
  output out_6,
  output out_7,
  output out_8,
  output out_9,
  output out_10,
  output out_11,
  output out_12,
  output out_13
);

  wire and_2_out, and_3_out, and_4_out, and_5_out, not_1_out, not_2_out, not_3_out, or_1_out, or_2_out,
       or_3_out, or_4_out, or_5_out;

  and and_1 (out_5, not_1_out, and_2_out);
  and and_2 (and_2_out, out_8, out_7);
  or or_1 (or_1_out, and_2_out, in_2);
  not not_1 (not_1_out, in_4);
  \四位二进制可逆计数器置9  \u_四位二进制可逆计数器置9_1  (
    .CPU(and_3_out), .QA(out_9), .CPD(and_5_out), .QB(out_8), .QC(out_7), .QD(out_6), .CLR(or_1_out));  // open: 置9
  or or_2 (or_2_out, out_9, out_8, out_7, out_6);
  or or_3 (or_3_out, or_2_out, or_4_out);
  or or_4 (or_4_out, out_13, out_12, out_11, out_10);
  and and_3 (and_3_out, not_2_out, out_12, not_3_out, out_10);
  and and_4 (and_4_out, or_3_out, in_3, in_4);
  not not_2 (not_2_out, out_13);
  not not_3 (not_3_out, out_11);
  or or_5 (or_5_out, and_3_out, and_2_out, in_2);
  \四位二进制可逆计数器置9  \u_四位二进制可逆计数器置9_2  (
    .CPU(in_1), .QA(out_13), .CPD(and_4_out), .QB(out_12), .QC(out_11), .QD(out_10), .\置9 (and_5_out),
    .CLR(or_5_out));
  and and_5 (and_5_out, out_10, out_11, out_12, out_13);
endmodule

module \带校准功能六十进制计数器封装  (
  input  in_1,
  input  in_2,
  input  in_3,
  output out_4
);

  wire clock_1_out;
  wire [3:0] \带校准功能的六十进制计数器_1_out_9 , \带校准功能的六十进制计数器_1_out_13 ;

  \带校准功能的六十进制计数器  \u_带校准功能的六十进制计数器_1  (
    .out_5(out_4), .out_6(\带校准功能的六十进制计数器_1_out_9 [3]), .out_7(\带校准功能的六十进制计数器_1_out_9 [2]),
    .out_8(\带校准功能的六十进制计数器_1_out_9 [1]), .out_9(\带校准功能的六十进制计数器_1_out_9 [0]),
    .out_10(\带校准功能的六十进制计数器_1_out_13 [3]), .out_11(\带校准功能的六十进制计数器_1_out_13 [2]),
    .out_12(\带校准功能的六十进制计数器_1_out_13 [1]), .out_13(\带校准功能的六十进制计数器_1_out_13 [0]), .in_1(clock_1_out),
    .in_2(in_3), .in_3(in_2), .in_4(in_1));
  Hex_Digit_Display hex_digit_display_1 (.value(\带校准功能的六十进制计数器_1_out_9 ));  // open: dp
  Hex_Digit_Display hex_digit_display_2 (.value(\带校准功能的六十进制计数器_1_out_13 ));  // open: dp
  Clock clock_1 (.out(clock_1_out));
endmodule

module \带校准功能六十进制计数器测试  (
  input  in_1,
  input  in_2,
  input  in_3,
  input  in_4,
  output out_5
);

  wire clock_1_out;
  wire [3:0] \四位二进制可逆计数器置9_1_qa , \带校准功能的六十进制计数器_1_out_9 , \带校准功能的六十进制计数器_1_out_13 ;

  Hex_Digit_Display hex_digit_display_1 (.value(\四位二进制可逆计数器置9_1_qa ));  // open: dp
  \四位二进制可逆计数器置9  \u_四位二进制可逆计数器置9_1  (
    .CPU(out_5), .QA(\四位二进制可逆计数器置9_1_qa [0]), .CPD(in_4), .QB(\四位二进制可逆计数器置9_1_qa [1]),
    .QC(\四位二进制可逆计数器置9_1_qa [2]), .QD(\四位二进制可逆计数器置9_1_qa [3]), .CLR(in_3));  // open: 置9
  \带校准功能的六十进制计数器  \u_带校准功能的六十进制计数器_1  (
    .out_5(out_5), .out_6(\带校准功能的六十进制计数器_1_out_9 [3]), .out_7(\带校准功能的六十进制计数器_1_out_9 [2]),
    .out_8(\带校准功能的六十进制计数器_1_out_9 [1]), .out_9(\带校准功能的六十进制计数器_1_out_9 [0]),
    .out_10(\带校准功能的六十进制计数器_1_out_13 [3]), .out_11(\带校准功能的六十进制计数器_1_out_13 [2]),
    .out_12(\带校准功能的六十进制计数器_1_out_13 [1]), .out_13(\带校准功能的六十进制计数器_1_out_13 [0]), .in_1(clock_1_out),
    .in_2(in_3), .in_3(in_2), .in_4(in_1));
  Hex_Digit_Display hex_digit_display_2 (.value(\带校准功能的六十进制计数器_1_out_9 ));  // open: dp
  Hex_Digit_Display hex_digit_display_3 (.value(\带校准功能的六十进制计数器_1_out_13 ));  // open: dp
  Clock clock_1 (.out(clock_1_out));
endmodule

module \校准计数值的十二进制或二十四进制计数器  (
  input  set,
  input  Adj,
  input  cpu,
  input  clr,
  input  cpd,
  output out_6,
  output out_7,
  output out_8,
  output out_9,
  output out_10,
  output out_11,
  output out_12,
  output out_13,
  output out_14
);

  wire and_2_out, and_3_out, and_4_out, and_5_out, and_6_out, multiplexer_1_out, not_1_out, not_2_out,
       not_3_out, or_1_out, or_2_out, or_3_out, or_4_out, or_5_out;

  and and_1 (out_6, not_1_out, multiplexer_1_out);
  Multiplexer #(.enable("false")) multiplexer_1 (.in0(and_2_out), .in1(and_3_out), .out(multiplexer_1_out), .sel(set));
  and and_2 (and_2_out, out_10, out_13);
  and and_3 (and_3_out, out_9, out_12);
  or or_1 (or_1_out, multiplexer_1_out, clr);
  not not_1 (not_1_out, Adj);
  \四位二进制可逆计数器置9  \u_四位二进制可逆计数器置9_1  (
    .CPU(and_4_out), .QA(out_10), .CPD(and_6_out), .QB(out_9), .QC(out_8), .QD(out_7), .CLR(or_1_out));  // open: 置9
  and and_4 (and_4_out, not_2_out, out_13, not_3_out, out_11);
  not not_2 (not_2_out, out_14);
  not not_3 (not_3_out, out_12);
  or or_2 (or_2_out, and_4_out, clr, multiplexer_1_out);
  and and_5 (and_5_out, cpd, Adj, or_5_out);
  \四位二进制可逆计数器置9  \u_四位二进制可逆计数器置9_2  (
    .CPU(cpu), .QA(out_14), .CPD(and_5_out), .QB(out_13), .QC(out_12), .QD(out_11), .\置9 (and_6_out),
    .CLR(or_2_out));
  and and_6 (and_6_out, out_11, out_12, out_13, out_14);
  or or_3 (or_3_out, out_10, out_9, out_8, out_7);
  or or_4 (or_4_out, out_14, out_13, out_12, out_11);
  or or_5 (or_5_out, or_3_out, or_4_out);
endmodule

module \校准计数值的十二进制或二十四进制计数器封装  (
  input  in_1,
  input  in_2,
  input  in_3,
  input  in_4,
  output out_5
);

  wire clock_1_out;
  wire [3:0] \校准计数值的十二进制或二十四进制计数器_1_out_10 , \校准计数值的十二进制或二十四进制计数器_1_out_14 ;

  Clock clock_1 (.out(clock_1_out));
  Hex_Digit_Display hex_digit_display_1 (.value(\校准计数值的十二进制或二十四进制计数器_1_out_10 ));  // open: dp
  Hex_Digit_Display hex_digit_display_2 (.value(\校准计数值的十二进制或二十四进制计数器_1_out_14 ));  // open: dp
  \校准计数值的十二进制或二十四进制计数器  \u_校准计数值的十二进制或二十四进制计数器_1  (
    .out_6(out_5), .out_7(\校准计数值的十二进制或二十四进制计数器_1_out_10 [3]), .out_8(\校准计数值的十二进制或二十四进制计数器_1_out_10 [2]),
    .out_9(\校准计数值的十二进制或二十四进制计数器_1_out_10 [1]), .out_10(\校准计数值的十二进制或二十四进制计数器_1_out_10 [0]),
    .out_11(\校准计数值的十二进制或二十四进制计数器_1_out_14 [3]), .out_12(\校准计数值的十二进制或二十四进制计数器_1_out_14 [2]),
    .out_13(\校准计数值的十二进制或二十四进制计数器_1_out_14 [1]), .out_14(\校准计数值的十二进制或二十四进制计数器_1_out_14 [0]), .set(in_2),
    .Adj(in_1), .cpu(clock_1_out), .clr(in_4), .cpd(in_3));
endmodule

module \带校准功能十二进制或者二十四进制测试  (
  input  in_1,
  input  in_2,
  input  in_3,
  input  in_4,
  input  in_5,
  input  in_6,
  input  in_7,
  output out_8
);

  wire clock_1_out;
  wire [3:0] \四位二进制可逆计数器置9_1_qa , \校准计数值的十二进制或二十四进制计数器_1_out_10 , \校准计数值的十二进制或二十四进制计数器_1_out_14 ;

  Clock clock_1 (.out(clock_1_out));
  Hex_Digit_Display hex_digit_display_1 (.value(\校准计数值的十二进制或二十四进制计数器_1_out_10 ));  // open: dp
  Hex_Digit_Display hex_digit_display_2 (.value(\校准计数值的十二进制或二十四进制计数器_1_out_14 ));  // open: dp
  \校准计数值的十二进制或二十四进制计数器  \u_校准计数值的十二进制或二十四进制计数器_1  (
    .out_6(out_8), .out_7(\校准计数值的十二进制或二十四进制计数器_1_out_10 [3]), .out_8(\校准计数值的十二进制或二十四进制计数器_1_out_10 [2]),
    .out_9(\校准计数值的十二进制或二十四进制计数器_1_out_10 [1]), .out_10(\校准计数值的十二进制或二十四进制计数器_1_out_10 [0]),
    .out_11(\校准计数值的十二进制或二十四进制计数器_1_out_14 [3]), .out_12(\校准计数值的十二进制或二十四进制计数器_1_out_14 [2]),
    .out_13(\校准计数值的十二进制或二十四进制计数器_1_out_14 [1]), .out_14(\校准计数值的十二进制或二十四进制计数器_1_out_14 [0]), .set(in_2),
    .Adj(in_1), .cpu(clock_1_out), .clr(in_4), .cpd(in_3));
  Hex_Digit_Display hex_digit_display_3 (.value(\四位二进制可逆计数器置9_1_qa ));  // open: dp
  \四位二进制可逆计数器置9  \u_四位二进制可逆计数器置9_1  (
    .CPU(out_8), .QA(\四位二进制可逆计数器置9_1_qa [0]), .CPD(in_6), .QB(\四位二进制可逆计数器置9_1_qa [1]),
    .QC(\四位二进制可逆计数器置9_1_qa [2]), .QD(\四位二进制可逆计数器置9_1_qa [3]), .\置9 (in_7), .CLR(in_5));
endmodule

module \显示上午下午电路  (
  input  TT,
  input  AM_FM,
  output [4:0] out_3,
  output [4:0] out_4,
  output [4:0] out_5,
  output [4:0] out_6
);

  wire [19:0] multiplexer_1_out, multiplexer_2_out;

  Multiplexer #(.width(20), .enable("false")) multiplexer_1 (
    .in0({20{1'b0}}), .in1(20'hfca1), .out(multiplexer_1_out), .sel(TT));
  Multiplexer #(.width(20), .enable("false")) multiplexer_2 (
    .in0({20{1'b0}}), .in1(20'h87e90), .out(multiplexer_2_out), .sel(TT));
  Multiplexer #(.width(20), .enable("false")) multiplexer_3 (
    .in0(multiplexer_1_out), .in1(multiplexer_2_out), .out({out_3, out_4, out_5, out_6}), .sel(AM_FM));
endmodule

module \显示上午下午电路测试  (
  input  in_1,
  input  in_2
);

  wire [4:0] \显示上午下午电路_1_out_3 , \显示上午下午电路_1_out_4 , \显示上午下午电路_1_out_5 , \显示上午下午电路_1_out_6 ;

  \显示上午下午电路  \u_显示上午下午电路_1  (
    .out_3(\显示上午下午电路_1_out_3 ), .out_4(\显示上午下午电路_1_out_4 ), .out_5(\显示上午下午电路_1_out_5 ),
    .out_6(\显示上午下午电路_1_out_6 ), .TT(in_2), .AM_FM(in_1));
  DotMatrix #(.matrixcols(4), .matrixrows(5)) dotmatrix_1 (
    .col0(\显示上午下午电路_1_out_3 ), .col1(\显示上午下午电路_1_out_4 ), .col2(\显示上午下午电路_1_out_5 ), .col3(\显示上午下午电路_1_out_6 ));
endmodule

module \电子钟整点报时电路  (
  input  in_1,
  input  in_2,
  input  in_3,
  input  in_4,
  input  in_5,
  input  in_6,
  input  in_7,
  input  in_8,
  input  in_9,
  input  in_10,
  input  in_11,
  input  in_12,
  input  in_13,
  output [3:0] out_14,
  output [3:0] out_15,
  output [3:0] out_16,
  output [3:0] out_17,
  output [3:0] out_18,
  output [3:0] out_19,
  output out_20,
  output [4:0] out_21,
  output [4:0] out_22,
  output [4:0] out_23,
  output [4:0] out_24
);

  wire and_1_out, and_2_out, and_3_out, not_1_out, or_1_out, or_2_out, t_ff_1_q, \带校准功能的六十进制计数器_1_out_5 ,
       \带校准功能的六十进制计数器_2_out_5 , \校准计数值的十二进制或二十四进制计数器_1_out_6 ;

  \校准计数值的十二进制或二十四进制计数器  \u_校准计数值的十二进制或二十四进制计数器_1  (
    .out_6(\校准计数值的十二进制或二十四进制计数器_1_out_6 ), .out_7(out_14[3]), .out_8(out_14[2]), .out_9(out_14[1]),
    .out_10(out_14[0]), .out_11(out_15[3]), .out_12(out_15[2]), .out_13(out_15[1]), .out_14(out_15[0]),
    .set(in_5), .Adj(in_4), .cpu(or_1_out), .clr(in_13), .cpd(in_12));
  T_Flip_Flop #(.trigger("falling")) t_ff_1 (
    .clk(\校准计数值的十二进制或二十四进制计数器_1_out_6 ), .T(1'b1), .Q(t_ff_1_q));  // open: Qn, preset, reset, en
  or or_1 (or_1_out, in_1, \带校准功能的六十进制计数器_1_out_5 );
  not not_1 (not_1_out, in_5);
  \带校准功能的六十进制计数器  \u_带校准功能的六十进制计数器_1  (
    .out_5(\带校准功能的六十进制计数器_1_out_5 ), .out_6(out_16[3]), .out_7(out_16[2]), .out_8(out_16[1]),
    .out_9(out_16[0]), .out_10(out_17[3]), .out_11(out_17[2]), .out_12(out_17[1]), .out_13(out_17[0]),
    .in_1(or_2_out), .in_2(in_9), .in_3(in_8), .in_4(in_6));
  \显示上午下午电路  \u_显示上午下午电路_1  (
    .out_3(out_21), .out_4(out_22), .out_5(out_23), .out_6(out_24), .TT(not_1_out), .AM_FM(t_ff_1_q));
  or or_2 (or_2_out, in_2, \带校准功能的六十进制计数器_2_out_5 );
  \带校准功能的六十进制计数器  \u_带校准功能的六十进制计数器_2  (
    .out_5(\带校准功能的六十进制计数器_2_out_5 ), .out_6(out_18[3]), .out_7(out_18[2]), .out_8(out_18[1]),
    .out_9(out_18[0]), .out_10(out_19[3]), .out_11(out_19[2]), .out_12(out_19[1]), .out_13(out_19[0]),
    .in_1(in_3), .in_2(in_11), .in_3(in_10), .in_4(in_7));
  and and_1 (and_1_out, out_16[2], out_16[0], out_17[3], out_17[0]);
  and and_2 (and_2_out, out_18[2], out_18[0]);
  and and_3 (and_3_out, and_1_out, and_2_out);
  and and_4 (out_20, and_3_out, out_19[0]);
endmodule

module \电子钟整点报时电路测试  (
  input  in_1,
  input  in_2,
  input  in_3,
  input  in_4,
  input  in_5,
  input  in_6,
  input  in_7,
  input  in_8,
  input  in_9,
  input  in_10,
  input  in_11,
  input  in_12,
  output out_13
);

  wire clock_1_out;
  wire [3:0] \电子钟整点报时电路_1_out_14 , \电子钟整点报时电路_1_out_15 , \电子钟整点报时电路_1_out_16 , \电子钟整点报时电路_1_out_17 ,
       \电子钟整点报时电路_1_out_18 , \电子钟整点报时电路_1_out_19 ;
  wire [4:0] \电子钟整点报时电路_1_out_21 , \电子钟整点报时电路_1_out_22 , \电子钟整点报时电路_1_out_23 , \电子钟整点报时电路_1_out_24 ;

  DotMatrix #(.matrixcols(4), .matrixrows(5)) dotmatrix_1 (
    .col0(\电子钟整点报时电路_1_out_21 ), .col1(\电子钟整点报时电路_1_out_22 ), .col2(\电子钟整点报时电路_1_out_23 ),
    .col3(\电子钟整点报时电路_1_out_24 ));
  \电子钟整点报时电路  \u_电子钟整点报时电路_1  (
    .in_4(in_1), .in_6(in_6), .in_7(in_10), .in_8(in_7), .in_10(in_11), .in_12(in_2), .in_1(in_3),
    .in_2(in_8), .in_3(clock_1_out), .in_5(in_5), .in_9(in_9), .in_11(in_12), .in_13(in_4),
    .out_21(\电子钟整点报时电路_1_out_21 ), .out_22(\电子钟整点报时电路_1_out_22 ), .out_23(\电子钟整点报时电路_1_out_23 ),
    .out_24(\电子钟整点报时电路_1_out_24 ), .out_14(\电子钟整点报时电路_1_out_14 ), .out_15(\电子钟整点报时电路_1_out_15 ),
    .out_16(\电子钟整点报时电路_1_out_16 ), .out_17(\电子钟整点报时电路_1_out_17 ), .out_18(\电子钟整点报时电路_1_out_18 ),
    .out_19(\电子钟整点报时电路_1_out_19 ), .out_20(out_13));
  Hex_Digit_Display hex_digit_display_1 (.value(\电子钟整点报时电路_1_out_15 ));  // open: dp
  Hex_Digit_Display hex_digit_display_2 (.value(\电子钟整点报时电路_1_out_14 ));  // open: dp
  Hex_Digit_Display hex_digit_display_3 (.value(\电子钟整点报时电路_1_out_16 ));  // open: dp
  Hex_Digit_Display hex_digit_display_4 (.value(\电子钟整点报时电路_1_out_17 ));  // open: dp
  Hex_Digit_Display hex_digit_display_5 (.value(\电子钟整点报时电路_1_out_18 ));  // open: dp
  Clock clock_1 (.out(clock_1_out));
  Hex_Digit_Display hex_digit_display_6 (.value(\电子钟整点报时电路_1_out_19 ));  // open: dp
endmodule

module \秒计时脉冲产生电路  (
  input  in_1,
  output out_2
);

  \四位二进制可逆计数器置9  \u_四位二进制可逆计数器置9_1  (.CPU(in_1), .CPD(1'b0), .QD(out_2), .\置9 (1'b0), .CLR(out_2));  // open: QA, QB, QC
endmodule

module \多功能数字钟电路  (
  input  in_1,
  input  in_2,
  input  CPD,
  input  CPU,
  input  Adj1,
  input  CP,
  input  Adj0,
  output [4:0] out_8,
  output [4:0] out_9,
  output [4:0] out_10,
  output [4:0] out_11,
  output out_12,
  output [3:0] out_13,
  output [3:0] out_14,
  output [3:0] out_15,
  output [3:0] out_16,
  output [3:0] out_17,
  output [3:0] out_18
);

  wire and_1_out, and_2_out, and_3_out, and_4_out, and_5_out, and_6_out, and_7_out, and_8_out, and_9_out,
       and_10_out, and_11_out, and_12_out, and_14_out, not_1_out, not_2_out, not_3_out, or_1_out, or_2_out,
       or_3_out, t_ff_1_q, \带校准功能的六十进制计数器_1_out_5 , \带校准功能的六十进制计数器_2_out_5 , \校准计数值的十二进制或二十四进制计数器_1_out_6 ,
       \秒计时脉冲产生电路_1_out_2 ;
  wire [3:0] adder_1_out, adder_2_out, \校准计数值的十二进制或二十四进制计数器_1_out_10 , \校准计数值的十二进制或二十四进制计数器_1_out_14 ;

  and and_1 (and_1_out, in_2, t_ff_1_q);
  not not_1 (not_1_out, Adj1);
  and and_2 (and_2_out, CPD, Adj0, not_1_out);
  not not_2 (not_2_out, Adj0);
  or or_1 (or_1_out, and_1_out, \校准计数值的十二进制或二十四进制计数器_1_out_6 );
  and and_3 (and_3_out, not_2_out, CP);
  T_Flip_Flop #(.trigger("falling")) t_ff_1 (.clk(or_1_out), .T(1'b1), .Q(t_ff_1_q));  // open: Qn, preset, reset, en
  Adder #(.width(4)) adder_1 (.a(4'b0001), .b(\校准计数值的十二进制或二十四进制计数器_1_out_10 ), .out(adder_1_out));  // open: cin, cout
  \显示上午下午电路  \u_显示上午下午电路_1  (
    .out_3(out_8), .out_4(out_9), .out_5(out_10), .out_6(out_11), .TT(not_3_out), .AM_FM(t_ff_1_q));
  Multiplexer #(.width(4), .enable("false")) multiplexer_1 (
    .in0(\校准计数值的十二进制或二十四进制计数器_1_out_10 ), .in1(adder_1_out), .out(out_13), .sel(and_5_out));
  not not_3 (not_3_out, in_1);
  \校准计数值的十二进制或二十四进制计数器  \u_校准计数值的十二进制或二十四进制计数器_1  (
    .out_6(\校准计数值的十二进制或二十四进制计数器_1_out_6 ), .out_7(\校准计数值的十二进制或二十四进制计数器_1_out_10 [3]),
    .out_8(\校准计数值的十二进制或二十四进制计数器_1_out_10 [2]), .out_9(\校准计数值的十二进制或二十四进制计数器_1_out_10 [1]),
    .out_10(\校准计数值的十二进制或二十四进制计数器_1_out_10 [0]), .out_11(\校准计数值的十二进制或二十四进制计数器_1_out_14 [3]),
    .out_12(\校准计数值的十二进制或二十四进制计数器_1_out_14 [2]), .out_13(\校准计数值的十二进制或二十四进制计数器_1_out_14 [1]),
    .out_14(\校准计数值的十二进制或二十四进制计数器_1_out_14 [0]), .set(in_1), .Adj(Adj0), .cpu(or_2_out), .clr(and_4_out),
    .cpd(and_2_out));
  and and_4 (and_4_out, in_2, not_1_out, Adj0);
  Adder #(.width(4)) adder_2 (.a(4'b0010), .b(\校准计数值的十二进制或二十四进制计数器_1_out_14 ), .out(adder_2_out));  // open: cin, cout
  and and_5 (and_5_out, in_1, t_ff_1_q);
  and and_6 (and_6_out, Adj0, not_1_out, CPU);
  or or_2 (or_2_out, and_6_out, \带校准功能的六十进制计数器_1_out_5 );
  Multiplexer #(.width(4), .enable("false")) multiplexer_2 (
    .in0(\校准计数值的十二进制或二十四进制计数器_1_out_14 ), .in1(adder_2_out), .out(out_14), .sel(and_5_out));
  \秒计时脉冲产生电路  \u_秒计时脉冲产生电路_1  (.in_1(and_3_out), .out_2(\秒计时脉冲产生电路_1_out_2 ));
  \带校准功能的六十进制计数器  \u_带校准功能的六十进制计数器_1  (
    .out_5(\带校准功能的六十进制计数器_1_out_5 ), .out_6(out_15[3]), .out_7(out_15[2]), .out_8(out_15[1]),
    .out_9(out_15[0]), .out_10(out_16[3]), .out_11(out_16[2]), .out_12(out_16[1]), .out_13(out_16[0]),
    .in_1(or_3_out), .in_2(and_10_out), .in_3(and_7_out), .in_4(Adj0));
  and and_7 (and_7_out, CPD, Adj0, Adj1);
  and and_8 (and_8_out, out_15[2], out_15[0], out_16[3], out_16[0]);
  and and_9 (and_9_out, Adj0, Adj1, CPU);
  or or_3 (or_3_out, and_9_out, \带校准功能的六十进制计数器_2_out_5 );
  and and_10 (and_10_out, in_2, Adj0, Adj1);
  and and_11 (and_11_out, and_8_out, and_12_out);
  and and_12 (and_12_out, out_17[0], out_17[2]);
  \带校准功能的六十进制计数器  \u_带校准功能的六十进制计数器_2  (
    .out_5(\带校准功能的六十进制计数器_2_out_5 ), .out_6(out_17[3]), .out_7(out_17[2]), .out_8(out_17[1]),
    .out_9(out_17[0]), .out_10(out_18[3]), .out_11(out_18[2]), .out_12(out_18[1]), .out_13(out_18[0]),
    .in_1(\秒计时脉冲产生电路_1_out_2 ), .in_2(and_14_out), .in_3(1'b0), .in_4(Adj0));
  and and_13 (out_12, and_11_out, out_18[0]);
  and and_14 (and_14_out, in_2, Adj0);
endmodule

module \测试  (
  input  in_1,
  input  in_2,
  input  in_3,
  input  in_4,
  input  in_5,
  input  in_6,
  output out_7
);

  wire clock_1_out;
  wire [3:0] \多功能数字钟电路_1_out_13 , \多功能数字钟电路_1_out_14 , \多功能数字钟电路_1_out_15 , \多功能数字钟电路_1_out_16 ,
       \多功能数字钟电路_1_out_17 , \多功能数字钟电路_1_out_18 ;
  wire [4:0] \多功能数字钟电路_1_out_8 , \多功能数字钟电路_1_out_9 , \多功能数字钟电路_1_out_10 , \多功能数字钟电路_1_out_11 ;

  DotMatrix #(.matrixcols(4), .matrixrows(5)) dotmatrix_1 (
    .col0(\多功能数字钟电路_1_out_8 ), .col1(\多功能数字钟电路_1_out_9 ), .col2(\多功能数字钟电路_1_out_10 ),
    .col3(\多功能数字钟电路_1_out_11 ));
  \多功能数字钟电路  \u_多功能数字钟电路_1  (
    .CP(clock_1_out), .out_8(\多功能数字钟电路_1_out_8 ), .out_9(\多功能数字钟电路_1_out_9 ), .out_10(\多功能数字钟电路_1_out_10 ),
    .out_11(\多功能数字钟电路_1_out_11 ), .in_1(in_5), .in_2(in_6), .CPD(in_4), .CPU(in_3),
    .out_13(\多功能数字钟电路_1_out_13 ), .out_14(\多功能数字钟电路_1_out_14 ), .out_15(\多功能数字钟电路_1_out_15 ),
    .out_16(\多功能数字钟电路_1_out_16 ), .out_17(\多功能数字钟电路_1_out_17 ), .out_18(\多功能数字钟电路_1_out_18 ), .out_12(out_7),
    .Adj0(in_1), .Adj1(in_2));
  Clock clock_1 (.out(clock_1_out));
  Hex_Digit_Display hex_digit_display_1 (.value(\多功能数字钟电路_1_out_13 ));  // open: dp
  Hex_Digit_Display hex_digit_display_2 (.value(\多功能数字钟电路_1_out_14 ));  // open: dp
  Hex_Digit_Display hex_digit_display_3 (.value(\多功能数字钟电路_1_out_15 ));  // open: dp
  Hex_Digit_Display hex_digit_display_4 (.value(\多功能数字钟电路_1_out_16 ));  // open: dp
  Hex_Digit_Display hex_digit_display_5 (.value(\多功能数字钟电路_1_out_17 ));  // open: dp
  Hex_Digit_Display hex_digit_display_6 (.value(\多功能数字钟电路_1_out_18 ));  // open: dp
endmodule
