// Logisim project My.circ as structural Verilog: 17 circuits, main circuit 超前进位四位二进制并行加法器
module \一位二进制半加器  (
  input  A,
  input  B,
  output S,
  output C
);

  xor xor_1 (S, A, B);
  and and_1 (C, A, B);
endmodule

module \一位二进制全加器  (
  input  A,
  input  B,
  input  Ci,
  output S,
  output C
);

  wire and_1_out, and_2_out, and_3_out, xor_1_out;

  and and_1 (and_1_out, A, B);
  and and_2 (and_2_out, A, Ci);
  and and_3 (and_3_out, B, Ci);
  xor xor_1 (xor_1_out, A, B);
  xor xor_2 (S, xor_1_out, Ci);
  or or_1 (C, and_1_out, and_2_out, and_3_out);
endmodule

module \四位串行进位二进制加法器  (
  input  A0,
  input  B0,
  input  A1,
  input  B1,
  input  A2,
  input  B2,
  input  A3,
  input  B3,
  input  C0,
  output C4,
  output S3,
  output S0,
  output S1,
  output S2
);

  wire \一位二进制全加器_1_c , \一位二进制全加器_2_c , \一位二进制全加器_3_c ;

  \一位二进制全加器  \u_一位二进制全加器_1  (.A(A0), .B(B0), .Ci(C0), .S(S0), .C(\一位二进制全加器_1_c ));
  \一位二进制全加器  \u_一位二进制全加器_2  (.A(A1), .B(B1), .Ci(\一位二进制全加器_1_c ), .S(S1), .C(\一位二进制全加器_2_c ));
  \一位二进制全加器  \u_一位二进制全加器_3  (.A(A2), .B(B2), .Ci(\一位二进制全加器_2_c ), .S(S2), .C(\一位二进制全加器_3_c ));
  \一位二进制全加器  \u_一位二进制全加器_4  (.A(A3), .B(B3), .Ci(\一位二进制全加器_3_c ), .S(S3), .C(C4));
endmodule

module \超前进位四位二进制并行加法器  (
  input  A4,
  input  B4,
  input  A1,
  input  B1,
  input  A2,
  input  B2,
  input  A3,
  input  B3,
  input  C0,
  output C4,
  output S1,
  output S4,
  output S2,
  output S3
);

  wire and_1_out, and_2_out, and_3_out, and_4_out, and_5_out, and_6_out, and_7_out, and_8_out, and_9_out,
       and_10_out, and_11_out, and_12_out, and_13_out, and_14_out, or_1_out, or_2_out, or_3_out, xor_1_out,
       xor_2_out, xor_3_out, xor_4_out;

  xor xor_1 (xor_1_out, A1, B1);
  and and_1 (and_1_out, C0, xor_1_out);
  or or_1 (or_1_out, and_1_out, and_2_out);
  \一位二进制全加器  \u_一位二进制全加器_1  (.A(A1), .B(B1), .Ci(C0), .S(S1));  // open: C
  and and_2 (and_2_out, B1, A1);
  xor xor_2 (xor_2_out, A2, B2);
  and and_3 (and_3_out, C0, xor_1_out, xor_2_out);
  or or_2 (or_2_out, and_3_out, and_5_out, and_4_out);
  \一位二进制全加器  \u_一位二进制全加器_2  (.A(A2), .B(B2), .Ci(or_1_out), .S(S2));  // open: C
  and and_4 (and_4_out, B2, A2);
  and and_5 (and_5_out, xor_2_out, and_2_out);
  xor xor_3 (xor_3_out, A3, B3);
  and and_6 (and_6_out, C0, xor_1_out, xor_2_out, xor_3_out);
  or or_3 (or_3_out, and_6_out, and_8_out, and_9_out, and_7_out);
  \一位二进制全加器  \u_一位二进制全加器_3  (.A(A3), .B(B3), .Ci(or_2_out), .S(S3));  // open: C
  and and_7 (and_7_out, B3, A3);
  and and_8 (and_8_out, xor_3_out, xor_2_out, and_2_out);
  and and_9 (and_9_out, xor_3_out, and_4_out);
  xor xor_4 (xor_4_out, A4, B4);
  and and_10 (and_10_out, and_2_out, xor_2_out, xor_3_out, xor_4_out);
  and and_11 (and_11_out, C0, xor_1_out, xor_2_out, xor_3_out, xor_4_out);
  or or_4 (C4, and_11_out, and_10_out, and_13_out, and_14_out, and_12_out);
  \一位二进制全加器  \u_一位二进制全加器_4  (.A(A4), .B(B4), .Ci(or_3_out), .S(S4));  // open: C
  and and_12 (and_12_out, B4, A4);
  and and_13 (and_13_out, and_4_out, xor_3_out, xor_4_out);
  and and_14 (and_14_out, and_7_out, xor_4_out);

  // Notes on the sheet:
  //   P1
  //   G1
  //   C1
  //   P2
  //   G2
  //   C2
  //   P3
  //   G3
  //   P4
  //   C3
  //   G4
  //   C4
endmodule

module \超前进位四位二进制并行加法器封装  (
  input  C0,
  input  A4,
  input  A3,
  input  A2,
  input  A1,
  input  B4,
  input  B3,
  input  B2,
  input  B1,
  output S4,
  output S3,
  output S2,
  output S1,
  output C4
);

  \超前进位四位二进制并行加法器  \u_超前进位四位二进制并行加法器_1  (
    .C0(C0), .C4(C4), .A1(A1), .B1(B1), .A2(A2), .B2(B2), .A3(A3), .B3(B3), .A4(A4), .B4(B4), .S1(S1),
    .S2(S2), .S3(S3), .S4(S4));
endmodule

module \四位二进制可逆计数器  (
  input  CPU,
  input  CPD,
  input  CLR,
  output Q0,
  output Q1,
  output Q2,
  output Q3
);

  wire and_1_out, and_2_out, and_3_out, and_4_out, and_5_out, and_6_out, d_ff_1_qn, d_ff_2_qn, d_ff_3_qn,
       d_ff_4_qn, or_1_out, or_2_out, or_3_out, or_4_out;

  or or_1 (or_1_out, CPU, CPD);
  and and_1 (and_1_out, Q0, CPU);
  and and_2 (and_2_out, d_ff_1_qn, CPD);
  or or_2 (or_2_out, and_1_out, and_2_out);
  and and_3 (and_3_out, Q1, and_1_out);
  and and_4 (and_4_out, d_ff_2_qn, and_2_out);
  or or_3 (or_3_out, and_3_out, and_4_out);
  and and_5 (and_5_out, Q2, and_3_out);
  and and_6 (and_6_out, d_ff_3_qn, and_4_out);
  or or_4 (or_4_out, and_5_out, and_6_out);
  D_Flip_Flop #(.trigger("falling")) d_ff_1 (
    .clk(or_1_out), .D(d_ff_1_qn), .Q(Q0), .Qn(d_ff_1_qn), .reset(CLR));  // open: preset, en
  D_Flip_Flop #(.trigger("falling")) d_ff_2 (
    .clk(or_2_out), .D(d_ff_2_qn), .Q(Q1), .Qn(d_ff_2_qn), .reset(CLR));  // open: preset, en
  D_Flip_Flop #(.trigger("falling")) d_ff_3 (
    .clk(or_3_out), .D(d_ff_3_qn), .Q(Q2), .Qn(d_ff_3_qn), .reset(CLR));  // open: preset, en
  D_Flip_Flop #(.trigger("falling")) d_ff_4 (
    .clk(or_4_out), .D(d_ff_4_qn), .Q(Q3), .Qn(d_ff_4_qn), .reset(CLR));  // open: preset, en
endmodule

module \四位二进制可逆计数器封装  (
  input  CPU,
  input  CPD,
  input  CLR,
  output R0,
  output R1,
  output R2,
  output R3
);

  \四位二进制可逆计数器  \u_四位二进制可逆计数器_1  (.CPU(CPU), .CPD(CPD), .CLR(CLR), .Q0(R0), .Q1(R1), .Q2(R2), .Q3(R3));
endmodule

module \四位二进制数转8421码  (
  input  Q4,
  input  Q3,
  input  Q2,
  input  Q1,
  output S80,
  output S40,
  output S20,
  output S10,
  output S8,
  output S4,
  output S2,
  output S1
);

  wire and_1_out, or_1_out;

  \超前进位四位二进制并行加法器  \u_超前进位四位二进制并行加法器_1  (
    .C0(1'b0), .C4(S10), .A1(Q1), .B1(1'b0), .A2(Q2), .B2(and_1_out), .A3(Q3), .B3(and_1_out), .A4(Q4),
    .B4(1'b0), .S1(S1), .S2(S2), .S3(S4), .S4(S8));
  or or_1 (or_1_out, Q2, Q3);
  and and_1 (and_1_out, Q4, or_1_out);

  assign S20 = 1'b0;
  assign S40 = 1'b0;
  assign S80 = 1'b0;
endmodule

module \四位二进制转8421码封装  (
  input  Q4,
  input  Q3,
  input  Q2,
  input  Q1,
  output S8,
  output S7,
  output S6,
  output S5,
  output S4,
  output S3,
  output S2,
  output S1
);

  \四位二进制数转8421码  \u_四位二进制数转8421码_1  (
    .S8(S4), .S4(S3), .S2(S2), .S1(S1), .Q1(Q1), .Q4(Q4), .Q3(Q3), .Q2(Q2), .S10(S5), .S20(S6), .S40(S7),
    .S80(S8));
endmodule

module \_7段数码显示管  (
  input  A0,
  input  A1,
  input  A2,
  input  A3,
  output a,
  output b,
  output c,
  output d,
  output e,
  output f,
  output g
);

  wire and_1_out, and_2_out, and_3_out, and_4_out, and_5_out, and_6_out, and_7_out, and_8_out, and_9_out,
       and_10_out, and_11_out, and_12_out, and_13_out, and_14_out, and_15_out, and_16_out, and_17_out,
       and_18_out, and_19_out, and_20_out, and_21_out, and_22_out, and_23_out, and_24_out, and_25_out,
       not_1_out, not_2_out, not_3_out, not_4_out;

  not not_1 (not_1_out, A0);
  not not_2 (not_2_out, A1);
  not not_3 (not_3_out, A2);
  not not_4 (not_4_out, A3);
  and and_1 (and_1_out, not_1_out, not_2_out, not_3_out);
  and and_2 (and_2_out, A1, not_3_out, not_4_out);
  and and_3 (and_3_out, A0, A2, not_4_out);
  and and_4 (and_4_out, A0, A3, not_2_out);
  and and_5 (and_5_out, not_1_out, not_2_out);
  and and_6 (and_6_out, not_2_out, not_3_out);
  and and_7 (and_7_out, not_3_out, not_4_out);
  and and_8 (and_8_out, A0, A1, not_4_out);
  and and_9 (and_9_out, A0, not_3_out);
  and and_10 (and_10_out, not_3_out, not_2_out);
  and and_11 (and_11_out, not_4_out, A2);
  and and_12 (and_12_out, not_1_out, not_3_out);
  and and_13 (and_13_out, A0, not_2_out, A2);
  and and_14 (and_14_out, A0, A1, not_3_out);
  and and_15 (and_15_out, not_1_out, A1, A2);
  and and_16 (and_16_out, not_1_out, A0);
  and and_17 (and_17_out, not_1_out, not_3_out);
  and and_18 (and_18_out, not_1_out, not_2_out);
  and and_19 (and_19_out, not_1_out, A2);
  and and_20 (and_20_out, not_2_out, A2);
  and and_21 (and_21_out, not_3_out, not_2_out, A3);
  and and_22 (and_22_out, A2, not_2_out);
  and and_23 (and_23_out, A3, not_3_out);
  and and_24 (and_24_out, not_3_out, A1);
  and and_25 (and_25_out, not_1_out, A1);
  or or_1 (a, and_1_out, and_2_out, and_3_out, and_4_out);
  or or_2 (b, and_5_out, and_6_out, and_7_out, and_8_out);
  or or_3 (c, and_9_out, and_10_out, and_11_out);
  or or_4 (d, and_12_out, and_13_out, and_14_out, and_15_out);
  or or_5 (e, and_16_out, and_17_out);
  or or_6 (f, and_18_out, and_19_out, and_20_out, and_21_out);
  or or_7 (g, and_22_out, and_23_out, and_24_out, and_25_out);
endmodule

module \_7段译码器封装  (
  input  A3,
  input  A2,
  input  A1,
  input  A0
);

  wire \n7段数码显示管_1_a , \n7段数码显示管_1_b , \n7段数码显示管_1_c , \n7段数码显示管_1_d , \n7段数码显示管_1_e , \n7段数码显示管_1_f ,
       \n7段数码显示管_1_g ;

  \_7段数码显示管  \u_7段数码显示管_1  (
    .a(\n7段数码显示管_1_a ), .A0(A0), .A1(A1), .A2(A2), .b(\n7段数码显示管_1_b ), .A3(A3), .c(\n7段数码显示管_1_c ),
    .d(\n7段数码显示管_1_d ), .e(\n7段数码显示管_1_e ), .f(\n7段数码显示管_1_f ), .g(\n7段数码显示管_1_g ));
  _7_Segment_Display u_7_segment_display_1 (
    .g(\n7段数码显示管_1_g ), .f(\n7段数码显示管_1_f ), .a(\n7段数码显示管_1_a ), .b(\n7段数码显示管_1_b ), .e(\n7段数码显示管_1_e ),
    .d(\n7段数码显示管_1_d ), .c(\n7段数码显示管_1_c ), .dp(1'b0));
endmodule

module \_7段译码器输出人数  (
  input  Q4,
  input  Q3,
  input  Q2,
  input  Q1
);

  wire \n7段数码显示管_1_a , \n7段数码显示管_1_b , \n7段数码显示管_1_c , \n7段数码显示管_1_d , \n7段数码显示管_1_e , \n7段数码显示管_1_f ,
       \n7段数码显示管_1_g , \n7段数码显示管_2_a , \n7段数码显示管_2_b , \n7段数码显示管_2_c , \n7段数码显示管_2_d , \n7段数码显示管_2_e ,
       \n7段数码显示管_2_f , \n7段数码显示管_2_g , \四位二进制数转8421码_1_s1 , \四位二进制数转8421码_1_s2 , \四位二进制数转8421码_1_s4 ,
       \四位二进制数转8421码_1_s8 , \四位二进制数转8421码_1_s10 , \四位二进制数转8421码_1_s20 , \四位二进制数转8421码_1_s40 ,
       \四位二进制数转8421码_1_s80 ;

  \_7段数码显示管  \u_7段数码显示管_1  (
    .a(\n7段数码显示管_1_a ), .A0(\四位二进制数转8421码_1_s10 ), .A1(\四位二进制数转8421码_1_s20 ), .A2(\四位二进制数转8421码_1_s40 ),
    .b(\n7段数码显示管_1_b ), .A3(\四位二进制数转8421码_1_s80 ), .c(\n7段数码显示管_1_c ), .d(\n7段数码显示管_1_d ),
    .e(\n7段数码显示管_1_e ), .f(\n7段数码显示管_1_f ), .g(\n7段数码显示管_1_g ));
  _7_Segment_Display u_7_segment_display_1 (
    .g(\n7段数码显示管_1_g ), .f(\n7段数码显示管_1_f ), .a(\n7段数码显示管_1_a ), .b(\n7段数码显示管_1_b ), .e(\n7段数码显示管_1_e ),
    .d(\n7段数码显示管_1_d ), .c(\n7段数码显示管_1_c ), .dp(1'b0));
  \四位二进制数转8421码  \u_四位二进制数转8421码_1  (
    .S8(\四位二进制数转8421码_1_s8 ), .S4(\四位二进制数转8421码_1_s4 ), .S2(\四位二进制数转8421码_1_s2 ), .S1(\四位二进制数转8421码_1_s1 ),
    .Q1(Q1), .Q4(Q4), .Q3(Q3), .Q2(Q2), .S10(\四位二进制数转8421码_1_s10 ), .S20(\四位二进制数转8421码_1_s20 ),
    .S40(\四位二进制数转8421码_1_s40 ), .S80(\四位二进制数转8421码_1_s80 ));
  \_7段数码显示管  \u_7段数码显示管_2  (
    .a(\n7段数码显示管_2_a ), .A0(\四位二进制数转8421码_1_s1 ), .A1(\四位二进制数转8421码_1_s2 ), .A2(\四位二进制数转8421码_1_s4 ),
    .b(\n7段数码显示管_2_b ), .A3(\四位二进制数转8421码_1_s8 ), .c(\n7段数码显示管_2_c ), .d(\n7段数码显示管_2_d ), .e(\n7段数码显示管_2_e ),
    .f(\n7段数码显示管_2_f ), .g(\n7段数码显示管_2_g ));
  _7_Segment_Display u_7_segment_display_2 (
    .g(\n7段数码显示管_2_g ), .f(\n7段数码显示管_2_f ), .a(\n7段数码显示管_2_a ), .b(\n7段数码显示管_2_b ), .e(\n7段数码显示管_2_e ),
    .d(\n7段数码显示管_2_d ), .c(\n7段数码显示管_2_c ), .dp(1'b0));
endmodule

module \满员门禁不  (
  input  CPU,
  input  CPD,
  input  CLR,
  output WARNING,
  output Q3,
  output Q2,
  output Q1,
  output Q0
);

  wire and_2_out, and_3_out, not_1_out, \无人信号_out , \满员信号_out ;

  and and_1 (WARNING, CPU, \满员信号_out );
  and and_2 (and_2_out, not_1_out, CPU);
  and and_3 (and_3_out, \无人信号_out , CPD);
  not not_1 (not_1_out, \满员信号_out );
  or \u_无人信号  (\无人信号_out , Q0, Q1, Q2, Q3);
  and \u_满员信号  (\满员信号_out , Q0, Q1, Q2, Q3);
  \四位二进制可逆计数器  \u_四位二进制可逆计数器_1  (.CPU(and_2_out), .CPD(and_3_out), .CLR(CLR), .Q0(Q0), .Q1(Q1), .Q2(Q2), .Q3(Q3));
endmodule

module \满员门禁不封装  (
  input  DOWN,
  input  UP,
  input  in_3,
  output Q0,
  output Q1,
  output Q2,
  output Q3
);

  \满员门禁不  \u_满员门禁不_1  (.CPU(UP), .CPD(DOWN), .CLR(in_3), .Q3(Q3), .Q2(Q2), .Q1(Q1), .Q0(Q0));  // open: WARNING

  // Notes on the sheet:
  //   CLR
endmodule

module \门禁系统电路A  (
  input  DOWN,
  input  UP,
  input  CLR,
  output WARNING
);

  wire \n7段数码显示管_1_a , \n7段数码显示管_1_b , \n7段数码显示管_1_c , \n7段数码显示管_1_d , \n7段数码显示管_1_e , \n7段数码显示管_1_f ,
       \n7段数码显示管_1_g , \n7段数码显示管_2_a , \n7段数码显示管_2_b , \n7段数码显示管_2_c , \n7段数码显示管_2_d , \n7段数码显示管_2_e ,
       \n7段数码显示管_2_f , \n7段数码显示管_2_g , \四位二进制数转8421码_1_s1 , \四位二进制数转8421码_1_s2 , \四位二进制数转8421码_1_s4 ,
       \四位二进制数转8421码_1_s8 , \四位二进制数转8421码_1_s10 , \四位二进制数转8421码_1_s20 , \四位二进制数转8421码_1_s40 ,
       \四位二进制数转8421码_1_s80 , \满员门禁不_1_q0 , \满员门禁不_1_q1 , \满员门禁不_1_q2 , \满员门禁不_1_q3 ;

  \_7段数码显示管  \u_7段数码显示管_1  (
    .a(\n7段数码显示管_1_a ), .A0(\四位二进制数转8421码_1_s10 ), .A1(\四位二进制数转8421码_1_s20 ), .A2(\四位二进制数转8421码_1_s40 ),
    .b(\n7段数码显示管_1_b ), .A3(\四位二进制数转8421码_1_s80 ), .c(\n7段数码显示管_1_c ), .d(\n7段数码显示管_1_d ),
    .e(\n7段数码显示管_1_e ), .f(\n7段数码显示管_1_f ), .g(\n7段数码显示管_1_g ));
  _7_Segment_Display u_7_segment_display_1 (
    .g(\n7段数码显示管_1_g ), .f(\n7段数码显示管_1_f ), .a(\n7段数码显示管_1_a ), .b(\n7段数码显示管_1_b ), .e(\n7段数码显示管_1_e ),
    .d(\n7段数码显示管_1_d ), .c(\n7段数码显示管_1_c ), .dp(1'b0));
  \四位二进制数转8421码  \u_四位二进制数转8421码_1  (
    .S8(\四位二进制数转8421码_1_s8 ), .S4(\四位二进制数转8421码_1_s4 ), .S2(\四位二进制数转8421码_1_s2 ), .S1(\四位二进制数转8421码_1_s1 ),
    .Q1(\满员门禁不_1_q0 ), .Q4(\满员门禁不_1_q3 ), .Q3(\满员门禁不_1_q2 ), .Q2(\满员门禁不_1_q1 ), .S10(\四位二进制数转8421码_1_s10 ),
    .S20(\四位二进制数转8421码_1_s20 ), .S40(\四位二进制数转8421码_1_s40 ), .S80(\四位二进制数转8421码_1_s80 ));
  \_7段数码显示管  \u_7段数码显示管_2  (
    .a(\n7段数码显示管_2_a ), .A0(\四位二进制数转8421码_1_s1 ), .A1(\四位二进制数转8421码_1_s2 ), .A2(\四位二进制数转8421码_1_s4 ),
    .b(\n7段数码显示管_2_b ), .A3(\四位二进制数转8421码_1_s8 ), .c(\n7段数码显示管_2_c ), .d(\n7段数码显示管_2_d ), .e(\n7段数码显示管_2_e ),
    .f(\n7段数码显示管_2_f ), .g(\n7段数码显示管_2_g ));
  \满员门禁不  \u_满员门禁不_1  (
    .CPU(UP), .CPD(DOWN), .CLR(CLR), .WARNING(WARNING), .Q3(\满员门禁不_1_q3 ), .Q2(\满员门禁不_1_q2 ),
    .Q1(\满员门禁不_1_q1 ), .Q0(\满员门禁不_1_q0 ));
  _7_Segment_Display u_7_segment_display_2 (
    .g(\n7段数码显示管_2_g ), .f(\n7段数码显示管_2_f ), .a(\n7段数码显示管_2_a ), .b(\n7段数码显示管_2_b ), .e(\n7段数码显示管_2_e ),
    .d(\n7段数码显示管_2_d ), .c(\n7段数码显示管_2_c ), .dp(1'b0));
endmodule

module \门禁电路封装B  (
  input  DOWN,
  input  UP,
  input  CLR,
  output A,
  output B,
  output C,
  output D,
  output E,
  output F,
  output G,
  output A_2,
  output B_2,
  output C_2,
  output D_2,
  output E_2,
  output F_2,
  output G_2,
  output WARNING
);

  wire \四位二进制数转8421码_1_s1 , \四位二进制数转8421码_1_s2 , \四位二进制数转8421码_1_s4 , \四位二进制数转8421码_1_s8 ,
       \四位二进制数转8421码_1_s10 , \四位二进制数转8421码_1_s20 , \四位二进制数转8421码_1_s40 , \四位二进制数转8421码_1_s80 , \满员门禁不_1_q0 ,
       \满员门禁不_1_q1 , \满员门禁不_1_q2 , \满员门禁不_1_q3 ;

  \_7段数码显示管  \u_7段数码显示管_1  (
    .a(A), .A0(\四位二进制数转8421码_1_s10 ), .A1(\四位二进制数转8421码_1_s20 ), .A2(\四位二进制数转8421码_1_s40 ), .b(B),
    .A3(\四位二进制数转8421码_1_s80 ), .c(C), .d(D), .e(E), .f(F), .g(G));
  \四位二进制数转8421码  \u_四位二进制数转8421码_1  (
    .S8(\四位二进制数转8421码_1_s8 ), .S4(\四位二进制数转8421码_1_s4 ), .S2(\四位二进制数转8421码_1_s2 ), .S1(\四位二进制数转8421码_1_s1 ),
    .Q1(\满员门禁不_1_q0 ), .Q4(\满员门禁不_1_q3 ), .Q3(\满员门禁不_1_q2 ), .Q2(\满员门禁不_1_q1 ), .S10(\四位二进制数转8421码_1_s10 ),
    .S20(\四位二进制数转8421码_1_s20 ), .S40(\四位二进制数转8421码_1_s40 ), .S80(\四位二进制数转8421码_1_s80 ));
  \_7段数码显示管  \u_7段数码显示管_2  (
    .a(A_2), .A0(\四位二进制数转8421码_1_s1 ), .A1(\四位二进制数转8421码_1_s2 ), .A2(\四位二进制数转8421码_1_s4 ), .b(B_2),
    .A3(\四位二进制数转8421码_1_s8 ), .c(C_2), .d(D_2), .e(E_2), .f(F_2), .g(G_2));
  \满员门禁不  \u_满员门禁不_1  (
    .CPU(UP), .CPD(DOWN), .CLR(CLR), .WARNING(WARNING), .Q3(\满员门禁不_1_q3 ), .Q2(\满员门禁不_1_q2 ),
    .Q1(\满员门禁不_1_q1 ), .Q0(\满员门禁不_1_q0 ));
endmodule

module \门禁电路封装C  (
  input  CPU,
  input  CLR,
  input  CPD,
  output WARNING
);

  wire \门禁电路封装b_1_a , \门禁电路封装b_1_a_2 , \门禁电路封装b_1_b , \门禁电路封装b_1_b_2 , \门禁电路封装b_1_c , \门禁电路封装b_1_c_2 ,
       \门禁电路封装b_1_d , \门禁电路封装b_1_d_2 , \门禁电路封装b_1_e , \门禁电路封装b_1_e_2 , \门禁电路封装b_1_f , \门禁电路封装b_1_f_2 ,
       \门禁电路封装b_1_g , \门禁电路封装b_1_g_2 ;

  \门禁电路封装B  \u_门禁电路封装b_1  (
    .WARNING(WARNING), .DOWN(CPD), .UP(CPU), .CLR(CLR), .A(\门禁电路封装b_1_a ), .B(\门禁电路封装b_1_b ),
    .C(\门禁电路封装b_1_c ), .D(\门禁电路封装b_1_d ), .E(\门禁电路封装b_1_e ), .F(\门禁电路封装b_1_f ), .G(\门禁电路封装b_1_g ),
    .A_2(\门禁电路封装b_1_a_2 ), .B_2(\门禁电路封装b_1_b_2 ), .C_2(\门禁电路封装b_1_c_2 ), .D_2(\门禁电路封装b_1_d_2 ),
    .E_2(\门禁电路封装b_1_e_2 ), .F_2(\门禁电路封装b_1_f_2 ), .G_2(\门禁电路封装b_1_g_2 ));
  _7_Segment_Display u_7_segment_display_1 (
    .g(\门禁电路封装b_1_g ), .f(\门禁电路封装b_1_f ), .a(\门禁电路封装b_1_a ), .b(\门禁电路封装b_1_b ), .e(\门禁电路封装b_1_e ),
    .d(\门禁电路封装b_1_d ), .c(\门禁电路封装b_1_c ), .dp(1'b0));
  _7_Segment_Display u_7_segment_display_2 (
    .g(\门禁电路封装b_1_g_2 ), .f(\门禁电路封装b_1_f_2 ), .a(\门禁电路封装b_1_a_2 ), .b(\门禁电路封装b_1_b_2 ), .e(\门禁电路封装b_1_e_2 ),
    .d(\门禁电路封装b_1_d_2 ), .c(\门禁电路封装b_1_c_2 ), .dp(1'b0));
endmodule
