// Logisim project My2.circ as structural Verilog: 17 circuits, main circuit 四输入8位宽加法器
module \四输入8位宽加法器  (
  input  [7:0] in_1,
  input  [7:0] in_2,
  input  [7:0] in_3,
  input  [7:0] in_4,
  output [7:0] out_5
);

  wire adder_1_cout;
  wire [7:0] adder_1_out, adder_2_out;

  Adder adder_1 (.a(in_1), .b(in_2), .out(adder_1_out), .cin(1'b0), .cout(adder_1_cout));
  Adder adder_2 (.a(in_3), .b(in_4), .out(adder_2_out), .cin(adder_1_cout));  // open: cout
  Adder adder_3 (.a(adder_1_out), .b(adder_2_out), .out(out_5), .cin(1'b0));  // open: cout
endmodule

module \无符号四位二进制乘法器  (
  input  [3:0] B0,
  input  [3:0] B1,
  output [7:0] R0
);

  wire [7:0] bit_extender_1_out, multiplexer_1_out, multiplexer_2_out, multiplexer_3_out, multiplexer_4_out,
       shifter_1_out, shifter_2_out, shifter_3_out;

  assign bit_extender_1_out = {{4{1'b0}}, B0};  // Bit_Extender bit_extender_1
  Multiplexer #(.width(8), .enable("false")) multiplexer_1 (
    .in0({8{1'b0}}), .in1(bit_extender_1_out), .out(multiplexer_1_out), .sel(B1[0]));
  Shifter shifter_1 (.in(bit_extender_1_out), .\dist (3'b001), .out(shifter_1_out));
  \四输入8位宽加法器  \u_四输入8位宽加法器_1  (
    .in_1(multiplexer_4_out), .in_2(multiplexer_3_out), .in_3(multiplexer_2_out), .in_4(multiplexer_1_out),
    .out_5(R0));
  Multiplexer #(.width(8), .enable("false")) multiplexer_2 (
    .in0({8{1'b0}}), .in1(shifter_1_out), .out(multiplexer_2_out), .sel(B1[1]));
  Shifter shifter_2 (.in(shifter_1_out), .\dist (3'b001), .out(shifter_2_out));
  Multiplexer #(.width(8), .enable("false")) multiplexer_3 (
    .in0({8{1'b0}}), .in1(shifter_2_out), .out(multiplexer_3_out), .sel(B1[2]));
  Shifter shifter_3 (.in(shifter_2_out), .\dist (3'b001), .out(shifter_3_out));
  Multiplexer #(.width(8), .enable("false")) multiplexer_4 (
    .in0({8{1'b0}}), .in1(shifter_3_out), .out(multiplexer_4_out), .sel(B1[3]));
endmodule

module \无符号四位二进制乘法器封装  (
  input  [3:0] a_3_0,
  input  [3:0] b_3_0,
  output [7:0] out_3
);

  \无符号四位二进制乘法器  \u_无符号四位二进制乘法器_1  (.B0(a_3_0), .B1(b_3_0), .R0(out_3));

  // Notes on the sheet:
  //   p(7:0)
endmodule

module \四输入32位宽加法器  (
  input  [31:0] in_1,
  input  [31:0] in_2,
  input  [31:0] in_3,
  input  [31:0] in_4,
  output [31:0] out_5
);

  wire adder_1_cout;
  wire [31:0] adder_1_out, adder_2_out;

  Adder #(.width(32)) adder_1 (.a(in_1), .b(in_2), .out(adder_1_out), .cin(1'b0), .cout(adder_1_cout));
  Adder #(.width(32)) adder_2 (.a(in_3), .b(in_4), .out(adder_2_out), .cin(adder_1_cout));  // open: cout
  Adder #(.width(32)) adder_3 (.a(adder_1_out), .b(adder_2_out), .out(out_5), .cin(1'b0));  // open: cout
endmodule

module \无符号32位_4位二进制乘法器  (
  input  [31:0] in_1,
  input  [3:0] B1_3_0,
  output [31:0] out_3
);

  wire [31:0] multiplexer_1_out, multiplexer_2_out, multiplexer_3_out, multiplexer_4_out, shifter_1_out,
       shifter_2_out, shifter_3_out;

  Multiplexer #(.width(32), .enable("false")) multiplexer_1 (
    .in0({32{1'b0}}), .in1(in_1), .out(multiplexer_1_out), .sel(B1_3_0[0]));
  \四输入32位宽加法器  \u_四输入32位宽加法器_1  (
    .in_1(multiplexer_1_out), .in_2(multiplexer_2_out), .in_3(multiplexer_3_out), .in_4(multiplexer_4_out),
    .out_5(out_3));
  Shifter #(.width(32)) shifter_1 (.in(in_1), .\dist (5'b00001), .out(shifter_1_out));
  Multiplexer #(.width(32), .enable("false")) multiplexer_2 (
    .in0({32{1'b0}}), .in1(shifter_1_out), .out(multiplexer_2_out), .sel(B1_3_0[1]));
  Shifter #(.width(32)) shifter_2 (.in(shifter_1_out), .\dist (5'b00001), .out(shifter_2_out));
  Multiplexer #(.width(32), .enable("false")) multiplexer_3 (
    .in0({32{1'b0}}), .in1(shifter_2_out), .out(multiplexer_3_out), .sel(B1_3_0[2]));
  Shifter #(.width(32)) shifter_3 (.in(shifter_2_out), .\dist (5'b00001), .out(shifter_3_out));
  Multiplexer #(.width(32), .enable("false")) multiplexer_4 (
    .in0({32{1'b0}}), .in1(shifter_3_out), .out(multiplexer_4_out), .sel(B1_3_0[3]));

  // Notes on the sheet:
  //   B0(31:0)
  //   R0(31:0)
endmodule

module \无符号32_4二进制乘法器封装  (
  input  [31:0] in_1,
  input  [3:0] a_3_0,
  output [31:0] out_3
);

  \无符号32位_4位二进制乘法器  \u_无符号32位_4位二进制乘法器_1  (.in_1(in_1), .B1_3_0(a_3_0), .out_3(out_3));

  // Notes on the sheet:
  //   b(31:0)
  //   p(31:0)
endmodule

module \八输入32位宽加法器  (
  input  [31:0] in_1,
  input  [31:0] in_2,
  input  [31:0] in_3,
  input  [31:0] in_4,
  input  [31:0] in_5,
  input  [31:0] in_6,
  input  [31:0] in_7,
  input  [31:0] in_8,
  output [31:0] out_9
);

  wire adder_1_cout, adder_3_cout;
  wire [31:0] adder_1_out, adder_2_out, adder_3_out, adder_4_out, adder_5_out, adder_6_out;

  Adder #(.width(32)) adder_1 (.a(in_1), .b(in_2), .out(adder_1_out), .cin(1'b0), .cout(adder_1_cout));
  Adder #(.width(32)) adder_2 (.a(in_3), .b(in_4), .out(adder_2_out), .cin(adder_1_cout));  // open: cout
  Adder #(.width(32)) adder_3 (.a(in_5), .b(in_6), .out(adder_3_out), .cin(1'b0), .cout(adder_3_cout));
  Adder #(.width(32)) adder_4 (.a(in_7), .b(in_8), .out(adder_4_out), .cin(adder_3_cout));  // open: cout
  Adder #(.width(32)) adder_5 (.a(adder_1_out), .b(adder_2_out), .out(adder_5_out), .cin(1'b0));  // open: cout
  Adder #(.width(32)) adder_6 (.a(adder_3_out), .b(adder_4_out), .out(adder_6_out), .cin(1'b0));  // open: cout
  Adder #(.width(32)) adder_7 (.a(adder_5_out), .b(adder_6_out), .out(out_9), .cin(1'b0));  // open: cout

  // Notes on the sheet:
  //   A0(31:0)
  //   A1(31:0)
  //   A2(31:0)
  //   A3(31:0)
  //   A4(31:0)
  //   A5(31:0)
  //   A6(31:0)
  //   A7(31:0)
  //   R0(31:0)
endmodule

module \无符号32_32位二进制乘法器  (
  input  [31:0] in_1,
  input  [31:0] in_2,
  output [31:0] out_3
);

  wire [31:0] shifter_1_out, shifter_2_out, shifter_3_out, shifter_4_out, shifter_5_out, shifter_6_out,
       shifter_7_out, \无符号32位_4位二进制乘法器_1_out_3 , \无符号32位_4位二进制乘法器_2_out_3 , \无符号32位_4位二进制乘法器_3_out_3 ,
       \无符号32位_4位二进制乘法器_4_out_3 , \无符号32位_4位二进制乘法器_5_out_3 , \无符号32位_4位二进制乘法器_6_out_3 ,
       \无符号32位_4位二进制乘法器_7_out_3 , \无符号32位_4位二进制乘法器_8_out_3 ;

  \无符号32位_4位二进制乘法器  \u_无符号32位_4位二进制乘法器_1  (.in_1(in_1), .B1_3_0(in_2[3:0]), .out_3(\无符号32位_4位二进制乘法器_1_out_3 ));
  \无符号32位_4位二进制乘法器  \u_无符号32位_4位二进制乘法器_2  (.in_1(in_1), .B1_3_0(in_2[7:4]), .out_3(\无符号32位_4位二进制乘法器_2_out_3 ));
  Shifter #(.width(32)) shifter_1 (.in(\无符号32位_4位二进制乘法器_2_out_3 ), .\dist (5'b00100), .out(shifter_1_out));
  \无符号32位_4位二进制乘法器  \u_无符号32位_4位二进制乘法器_3  (.in_1(in_1), .B1_3_0(in_2[11:8]), .out_3(\无符号32位_4位二进制乘法器_3_out_3 ));
  Shifter #(.width(32)) shifter_2 (.in(\无符号32位_4位二进制乘法器_3_out_3 ), .\dist (5'b01000), .out(shifter_2_out));
  \无符号32位_4位二进制乘法器  \u_无符号32位_4位二进制乘法器_4  (.in_1(in_1), .B1_3_0(in_2[15:12]), .out_3(\无符号32位_4位二进制乘法器_4_out_3 ));
  \八输入32位宽加法器  \u_八输入32位宽加法器_1  (
    .in_1(\无符号32位_4位二进制乘法器_1_out_3 ), .in_2(shifter_1_out), .in_3(shifter_2_out), .in_4(shifter_3_out),
    .in_5(shifter_4_out), .in_6(shifter_5_out), .in_7(shifter_6_out), .in_8(shifter_7_out), .out_9(out_3));
  Shifter #(.width(32)) shifter_3 (.in(\无符号32位_4位二进制乘法器_4_out_3 ), .\dist (5'b01100), .out(shifter_3_out));
  \无符号32位_4位二进制乘法器  \u_无符号32位_4位二进制乘法器_5  (.in_1(in_1), .B1_3_0(in_2[19:16]), .out_3(\无符号32位_4位二进制乘法器_5_out_3 ));
  Shifter #(.width(32)) shifter_4 (.in(\无符号32位_4位二进制乘法器_5_out_3 ), .\dist (5'b10000), .out(shifter_4_out));
  \无符号32位_4位二进制乘法器  \u_无符号32位_4位二进制乘法器_6  (.in_1(in_1), .B1_3_0(in_2[23:20]), .out_3(\无符号32位_4位二进制乘法器_6_out_3 ));
  Shifter #(.width(32)) shifter_5 (.in(\无符号32位_4位二进制乘法器_6_out_3 ), .\dist (5'b10100), .out(shifter_5_out));
  \无符号32位_4位二进制乘法器  \u_无符号32位_4位二进制乘法器_7  (.in_1(in_1), .B1_3_0(in_2[27:24]), .out_3(\无符号32位_4位二进制乘法器_7_out_3 ));
  Shifter #(.width(32)) shifter_6 (.in(\无符号32位_4位二进制乘法器_7_out_3 ), .\dist (5'b11000), .out(shifter_6_out));
  \无符号32位_4位二进制乘法器  \u_无符号32位_4位二进制乘法器_8  (.in_1(in_1), .B1_3_0(in_2[31:28]), .out_3(\无符号32位_4位二进制乘法器_8_out_3 ));
  Shifter #(.width(32)) shifter_7 (.in(\无符号32位_4位二进制乘法器_8_out_3 ), .\dist (5'b11100), .out(shifter_7_out));

  // Notes on the sheet:
  //   B0(31:0)
  //   B1(31:0)
  //   R0(31:0)
endmodule

module \八输入32位宽加法器2  (
  input  [31:0] in_1,
  input  [31:0] in_2,
  input  [31:0] in_3,
  input  [31:0] in_4,
  input  [31:0] in_5,
  input  [31:0] in_6,
  input  [31:0] in_7,
  input  [31:0] in_8,
  output [31:0] out_9
);

  wire [31:0] \四输入32位宽加法器_1_out_5 , \四输入32位宽加法器_2_out_5 ;

  \四输入32位宽加法器  \u_四输入32位宽加法器_1  (.in_1(in_1), .in_2(in_2), .in_3(in_3), .in_4(in_4), .out_5(\四输入32位宽加法器_1_out_5 ));
  \四输入32位宽加法器  \u_四输入32位宽加法器_2  (.in_1(in_5), .in_2(in_6), .in_3(in_7), .in_4(in_8), .out_5(\四输入32位宽加法器_2_out_5 ));
  Adder #(.width(32)) adder_1 (
    .a(\四输入32位宽加法器_1_out_5 ), .b(\四输入32位宽加法器_2_out_5 ), .out(out_9), .cin(1'b0));  // open: cout
endmodule

module \无符号32_32二进制乘法器封装  (
  input  [31:0] in_1,
  input  [31:0] in_2,
  output [31:0] out_3
);

  \无符号32_32位二进制乘法器  \u_无符号32_32位二进制乘法器_1  (.out_3(out_3), .in_1(in_1), .in_2(in_2));

  // Notes on the sheet:
  //   a(31:0)
  //   b(31:0)
  //   p(31:0)
endmodule

module \无符号四位二进制除法器  (
  input  [3:0] in_1,
  input  [3:0] in_2,
  output [3:0] out_3,
  output [3:0] out_4
);

  wire comparator_1_lt, comparator_2_lt, comparator_3_lt, comparator_4_lt;
  wire [3:0] subtractor_1_out, subtractor_2_out, subtractor_3_out, subtractor_4_out;
  wire [7:0] bit_extender_1_out, multiplexer_1_out, multiplexer_2_out, multiplexer_3_out, shifter_1_out,
       shifter_2_out, shifter_3_out, shifter_4_out;

  assign bit_extender_1_out = {{4{1'b0}}, in_1};  // Bit_Extender bit_extender_1
  Shifter shifter_1 (.in(bit_extender_1_out), .\dist (3'b001), .out(shifter_1_out));
  Subtractor #(.width(4)) subtractor_1 (
    .a(shifter_1_out[7:4]), .b(in_2), .out(subtractor_1_out), .bin(1'b0));  // open: bout
  Comparator #(.width(4), .mode("unsigned")) comparator_1 (
    .a(shifter_1_out[7:4]), .b(in_2), .lt(comparator_1_lt));  // open: gt, eq
  not not_1 (out_3[3], comparator_1_lt);
  Multiplexer #(.width(8), .enable("false")) multiplexer_1 (
    .in0({subtractor_1_out, shifter_1_out[3:0]}), .in1(shifter_1_out), .out(multiplexer_1_out),
    .sel(comparator_1_lt));
  Shifter shifter_2 (.in(multiplexer_1_out), .\dist (3'b001), .out(shifter_2_out));
  Subtractor #(.width(4)) subtractor_2 (
    .a(shifter_2_out[7:4]), .b(in_2), .out(subtractor_2_out), .bin(1'b0));  // open: bout
  Comparator #(.width(4), .mode("unsigned")) comparator_2 (
    .a(shifter_2_out[7:4]), .b(in_2), .lt(comparator_2_lt));  // open: gt, eq
  Multiplexer #(.width(8), .enable("false")) multiplexer_2 (
    .in0({subtractor_2_out, shifter_2_out[3:0]}), .in1(shifter_2_out), .out(multiplexer_2_out),
    .sel(comparator_2_lt));
  not not_2 (out_3[2], comparator_2_lt);
  Shifter shifter_3 (.in(multiplexer_2_out), .\dist (3'b001), .out(shifter_3_out));
  Subtractor #(.width(4)) subtractor_3 (
    .a(shifter_3_out[7:4]), .b(in_2), .out(subtractor_3_out), .bin(1'b0));  // open: bout
  Comparator #(.width(4), .mode("unsigned")) comparator_3 (
    .a(shifter_3_out[7:4]), .b(in_2), .lt(comparator_3_lt));  // open: gt, eq
  not not_3 (out_3[1], comparator_3_lt);
  Multiplexer #(.width(8), .enable("false")) multiplexer_3 (
    .in0({subtractor_3_out, shifter_3_out[3:0]}), .in1(shifter_3_out), .out(multiplexer_3_out),
    .sel(comparator_3_lt));
  Shifter shifter_4 (.in(multiplexer_3_out), .\dist (3'b001), .out(shifter_4_out));
  Subtractor #(.width(4)) subtractor_4 (
    .a(shifter_4_out[7:4]), .b(in_2), .out(subtractor_4_out), .bin(1'b0));  // open: bout
  Multiplexer #(.width(4), .enable("false")) multiplexer_4 (
    .in0(subtractor_4_out), .in1(shifter_4_out[7:4]), .out(out_4), .sel(comparator_4_lt));
  Comparator #(.width(4), .mode("unsigned")) comparator_4 (
    .a(shifter_4_out[7:4]), .b(in_2), .lt(comparator_4_lt));  // open: gt, eq
  not not_4 (out_3[0], comparator_4_lt);
endmodule

module \无符号四位二进制除法器封装  (
  input  [3:0] n2_3_0,
  input  [3:0] d_3_0,
  output [3:0] quot_3_0,
  output [3:0] rem_3_0
);

  \无符号四位二进制除法器  \u_无符号四位二进制除法器_1  (.in_1(n2_3_0), .in_2(d_3_0), .out_4(rem_3_0), .out_3(quot_3_0));
endmodule

module \无符号四位二进制模块  (
  input  [7:0] in_1,
  input  [3:0] in_2,
  output [7:0] out_3,
  output out_4
);

  wire comparator_1_lt;
  wire [3:0] subtractor_1_out;
  wire [7:0] shifter_1_out;

  Shifter shifter_1 (.in(in_1), .\dist (3'b001), .out(shifter_1_out));
  Subtractor #(.width(4)) subtractor_1 (
    .a(shifter_1_out[7:4]), .b(in_2), .out(subtractor_1_out), .bin(1'b0));  // open: bout
  Comparator #(.width(4), .mode("unsigned")) comparator_1 (
    .a(shifter_1_out[7:4]), .b(in_2), .lt(comparator_1_lt));  // open: gt, eq
  Multiplexer #(.width(8), .enable("false")) multiplexer_1 (
    .in0({subtractor_1_out, shifter_1_out[3:0]}), .in1(shifter_1_out), .out(out_3), .sel(comparator_1_lt));
  not not_1 (out_4, comparator_1_lt);
endmodule

module \无符号四位二进制模块化  (
  input  [3:0] n2_3_0,
  input  [3:0] d_3_0,
  output [3:0] rem_3_0,
  output [3:0] quot_3_0
);

  wire [3:0] \无符号四位二进制模块_4_out_3 ;
  wire [7:0] bit_extender_1_out, \无符号四位二进制模块_1_out_3 , \无符号四位二进制模块_2_out_3 , \无符号四位二进制模块_3_out_3 ;

  assign bit_extender_1_out = {{4{1'b0}}, n2_3_0};  // Bit_Extender bit_extender_1
  \无符号四位二进制模块  \u_无符号四位二进制模块_1  (
    .in_1(bit_extender_1_out), .in_2(d_3_0), .out_3(\无符号四位二进制模块_1_out_3 ), .out_4(quot_3_0[3]));
  \无符号四位二进制模块  \u_无符号四位二进制模块_2  (
    .in_1(\无符号四位二进制模块_1_out_3 ), .in_2(d_3_0), .out_3(\无符号四位二进制模块_2_out_3 ), .out_4(quot_3_0[2]));
  \无符号四位二进制模块  \u_无符号四位二进制模块_3  (
    .in_1(\无符号四位二进制模块_2_out_3 ), .in_2(d_3_0), .out_3(\无符号四位二进制模块_3_out_3 ), .out_4(quot_3_0[1]));
  \无符号四位二进制模块  \u_无符号四位二进制模块_4  (
    .in_1(\无符号四位二进制模块_3_out_3 ), .in_2(d_3_0), .out_3({rem_3_0, \无符号四位二进制模块_4_out_3 }), .out_4(quot_3_0[0]));
endmodule

module \无符号32位二进制除法器模块  (
  input  [31:0] in_1,
  input  [31:0] in_2,
  input  [31:0] in_3,
  output [31:0] out_4,
  output [31:0] out_5,
  output out_6
);

  wire comparator_1_gt;
  wire [31:0] subtractor_1_out;

  Shifter #(.width(32)) shifter_1 (.in(in_1), .\dist (5'b00001), .out(out_4));
  Subtractor #(.width(32)) subtractor_1 (
    .a({in_3[30:0], in_1[31]}), .b(in_2), .out(subtractor_1_out));  // open: bin, bout
  Comparator #(.width(32), .mode("unsigned")) comparator_1 (
    .a(in_2), .b({in_3[30:0], in_1[31]}), .gt(comparator_1_gt));  // open: eq, lt
  not not_1 (out_6, comparator_1_gt);
  Multiplexer #(.width(32), .enable("false")) multiplexer_1 (
    .in0(subtractor_1_out), .in1({in_3[30:0], in_1[31]}), .out(out_5), .sel(comparator_1_gt));

  // Notes on the sheet:
  //   n(31:0)
  //   d(31:0)
endmodule

module \无符号32位除法器  (
  input  [31:0] in_1,
  input  [31:0] in_2,
  output [31:0] out_3,
  output [31:0] out_4
);

  wire [31:0] \无符号32位二进制除法器模块_1_out_4 , \无符号32位二进制除法器模块_1_out_5 , \无符号32位二进制除法器模块_2_out_4 ,
       \无符号32位二进制除法器模块_2_out_5 , \无符号32位二进制除法器模块_3_out_4 , \无符号32位二进制除法器模块_3_out_5 ,
       \无符号32位二进制除法器模块_4_out_4 , \无符号32位二进制除法器模块_4_out_5 , \无符号32位二进制除法器模块_5_out_4 ,
       \无符号32位二进制除法器模块_5_out_5 , \无符号32位二进制除法器模块_6_out_4 , \无符号32位二进制除法器模块_6_out_5 ,
       \无符号32位二进制除法器模块_7_out_4 , \无符号32位二进制除法器模块_7_out_5 , \无符号32位二进制除法器模块_8_out_4 ,
       \无符号32位二进制除法器模块_8_out_5 , \无符号32位二进制除法器模块_9_out_4 , \无符号32位二进制除法器模块_9_out_5 ,
       \无符号32位二进制除法器模块_10_out_4 , \无符号32位二进制除法器模块_10_out_5 , \无符号32位二进制除法器模块_11_out_4 ,
       \无符号32位二进制除法器模块_11_out_5 , \无符号32位二进制除法器模块_12_out_4 , \无符号32位二进制除法器模块_12_out_5 ,
       \无符号32位二进制除法器模块_13_out_4 , \无符号32位二进制除法器模块_13_out_5 , \无符号32位二进制除法器模块_14_out_4 ,
       \无符号32位二进制除法器模块_14_out_5 , \无符号32位二进制除法器模块_15_out_4 , \无符号32位二进制除法器模块_15_out_5 ,
       \无符号32位二进制除法器模块_16_out_4 , \无符号32位二进制除法器模块_16_out_5 , \无符号32位二进制除法器模块_17_out_4 ,
       \无符号32位二进制除法器模块_17_out_5 , \无符号32位二进制除法器模块_18_out_4 , \无符号32位二进制除法器模块_18_out_5 ,
       \无符号32位二进制除法器模块_19_out_4 , \无符号32位二进制除法器模块_19_out_5 , \无符号32位二进制除法器模块_20_out_4 ,
       \无符号32位二进制除法器模块_20_out_5 , \无符号32位二进制除法器模块_21_out_4 , \无符号32位二进制除法器模块_21_out_5 ,
       \无符号32位二进制除法器模块_22_out_4 , \无符号32位二进制除法器模块_22_out_5 , \无符号32位二进制除法器模块_23_out_4 ,
       \无符号32位二进制除法器模块_23_out_5 , \无符号32位二进制除法器模块_24_out_4 , \无符号32位二进制除法器模块_24_out_5 ,
       \无符号32位二进制除法器模块_25_out_4 , \无符号32位二进制除法器模块_25_out_5 , \无符号32位二进制除法器模块_26_out_4 ,
       \无符号32位二进制除法器模块_26_out_5 , \无符号32位二进制除法器模块_27_out_4 , \无符号32位二进制除法器模块_27_out_5 ,
       \无符号32位二进制除法器模块_28_out_4 , \无符号32位二进制除法器模块_28_out_5 , \无符号32位二进制除法器模块_29_out_4 ,
       \无符号32位二进制除法器模块_29_out_5 , \无符号32位二进制除法器模块_30_out_4 , \无符号32位二进制除法器模块_30_out_5 ,
       \无符号32位二进制除法器模块_31_out_4 , \无符号32位二进制除法器模块_31_out_5 ;

  \无符号32位二进制除法器模块  \u_无符号32位二进制除法器模块_1  (
    .in_1(in_1), .in_2(in_2), .in_3({32{1'b0}}), .out_4(\无符号32位二进制除法器模块_1_out_4 ),
    .out_5(\无符号32位二进制除法器模块_1_out_5 ), .out_6(out_4[31]));
  \无符号32位二进制除法器模块  \u_无符号32位二进制除法器模块_2  (
    .in_1(\无符号32位二进制除法器模块_29_out_4 ), .in_2(in_2), .in_3(\无符号32位二进制除法器模块_29_out_5 ),
    .out_4(\无符号32位二进制除法器模块_2_out_4 ), .out_5(\无符号32位二进制除法器模块_2_out_5 ), .out_6(out_4[23]));
  \无符号32位二进制除法器模块  \u_无符号32位二进制除法器模块_3  (
    .in_1(\无符号32位二进制除法器模块_30_out_4 ), .in_2(in_2), .in_3(\无符号32位二进制除法器模块_30_out_5 ),
    .out_4(\无符号32位二进制除法器模块_3_out_4 ), .out_5(\无符号32位二进制除法器模块_3_out_5 ), .out_6(out_4[15]));
  \无符号32位二进制除法器模块  \u_无符号32位二进制除法器模块_4  (
    .in_1(\无符号32位二进制除法器模块_31_out_4 ), .in_2(in_2), .in_3(\无符号32位二进制除法器模块_31_out_5 ),
    .out_4(\无符号32位二进制除法器模块_4_out_4 ), .out_5(\无符号32位二进制除法器模块_4_out_5 ), .out_6(out_4[7]));
  \无符号32位二进制除法器模块  \u_无符号32位二进制除法器模块_5  (
    .in_1(\无符号32位二进制除法器模块_1_out_4 ), .in_2(in_2), .in_3(\无符号32位二进制除法器模块_1_out_5 ),
    .out_4(\无符号32位二进制除法器模块_5_out_4 ), .out_5(\无符号32位二进制除法器模块_5_out_5 ), .out_6(out_4[30]));
  \无符号32位二进制除法器模块  \u_无符号32位二进制除法器模块_6  (
    .in_1(\无符号32位二进制除法器模块_2_out_4 ), .in_2(in_2), .in_3(\无符号32位二进制除法器模块_2_out_5 ),
    .out_4(\无符号32位二进制除法器模块_6_out_4 ), .out_5(\无符号32位二进制除法器模块_6_out_5 ), .out_6(out_4[22]));
  \无符号32位二进制除法器模块  \u_无符号32位二进制除法器模块_7  (
    .in_1(\无符号32位二进制除法器模块_3_out_4 ), .in_2(in_2), .in_3(\无符号32位二进制除法器模块_3_out_5 ),
    .out_4(\无符号32位二进制除法器模块_7_out_4 ), .out_5(\无符号32位二进制除法器模块_7_out_5 ), .out_6(out_4[14]));
  \无符号32位二进制除法器模块  \u_无符号32位二进制除法器模块_8  (
    .in_1(\无符号32位二进制除法器模块_4_out_4 ), .in_2(in_2), .in_3(\无符号32位二进制除法器模块_4_out_5 ),
    .out_4(\无符号32位二进制除法器模块_8_out_4 ), .out_5(\无符号32位二进制除法器模块_8_out_5 ), .out_6(out_4[6]));
  \无符号32位二进制除法器模块  \u_无符号32位二进制除法器模块_9  (
    .in_1(\无符号32位二进制除法器模块_5_out_4 ), .in_2(in_2), .in_3(\无符号32位二进制除法器模块_5_out_5 ),
    .out_4(\无符号32位二进制除法器模块_9_out_4 ), .out_5(\无符号32位二进制除法器模块_9_out_5 ), .out_6(out_4[29]));
  \无符号32位二进制除法器模块  \u_无符号32位二进制除法器模块_10  (
    .in_1(\无符号32位二进制除法器模块_6_out_4 ), .in_2(in_2), .in_3(\无符号32位二进制除法器模块_6_out_5 ),
    .out_4(\无符号32位二进制除法器模块_10_out_4 ), .out_5(\无符号32位二进制除法器模块_10_out_5 ), .out_6(out_4[21]));
  \无符号32位二进制除法器模块  \u_无符号32位二进制除法器模块_11  (
    .in_1(\无符号32位二进制除法器模块_7_out_4 ), .in_2(in_2), .in_3(\无符号32位二进制除法器模块_7_out_5 ),
    .out_4(\无符号32位二进制除法器模块_11_out_4 ), .out_5(\无符号32位二进制除法器模块_11_out_5 ), .out_6(out_4[13]));
  \无符号32位二进制除法器模块  \u_无符号32位二进制除法器模块_12  (
    .in_1(\无符号32位二进制除法器模块_8_out_4 ), .in_2(in_2), .in_3(\无符号32位二进制除法器模块_8_out_5 ),
    .out_4(\无符号32位二进制除法器模块_12_out_4 ), .out_5(\无符号32位二进制除法器模块_12_out_5 ), .out_6(out_4[5]));
  \无符号32位二进制除法器模块  \u_无符号32位二进制除法器模块_13  (
    .in_1(\无符号32位二进制除法器模块_9_out_4 ), .in_2(in_2), .in_3(\无符号32位二进制除法器模块_9_out_5 ),
    .out_4(\无符号32位二进制除法器模块_13_out_4 ), .out_5(\无符号32位二进制除法器模块_13_out_5 ), .out_6(out_4[28]));
  \无符号32位二进制除法器模块  \u_无符号32位二进制除法器模块_14  (
    .in_1(\无符号32位二进制除法器模块_10_out_4 ), .in_2(in_2), .in_3(\无符号32位二进制除法器模块_10_out_5 ),
    .out_4(\无符号32位二进制除法器模块_14_out_4 ), .out_5(\无符号32位二进制除法器模块_14_out_5 ), .out_6(out_4[20]));
  \无符号32位二进制除法器模块  \u_无符号32位二进制除法器模块_15  (
    .in_1(\无符号32位二进制除法器模块_11_out_4 ), .in_2(in_2), .in_3(\无符号32位二进制除法器模块_11_out_5 ),
    .out_4(\无符号32位二进制除法器模块_15_out_4 ), .out_5(\无符号32位二进制除法器模块_15_out_5 ), .out_6(out_4[12]));
  \无符号32位二进制除法器模块  \u_无符号32位二进制除法器模块_16  (
    .in_1(\无符号32位二进制除法器模块_12_out_4 ), .in_2(in_2), .in_3(\无符号32位二进制除法器模块_12_out_5 ),
    .out_4(\无符号32位二进制除法器模块_16_out_4 ), .out_5(\无符号32位二进制除法器模块_16_out_5 ), .out_6(out_4[4]));
  \无符号32位二进制除法器模块  \u_无符号32位二进制除法器模块_17  (
    .in_1(\无符号32位二进制除法器模块_13_out_4 ), .in_2(in_2), .in_3(\无符号32位二进制除法器模块_13_out_5 ),
    .out_4(\无符号32位二进制除法器模块_17_out_4 ), .out_5(\无符号32位二进制除法器模块_17_out_5 ), .out_6(out_4[27]));
  \无符号32位二进制除法器模块  \u_无符号32位二进制除法器模块_18  (
    .in_1(\无符号32位二进制除法器模块_14_out_4 ), .in_2(in_2), .in_3(\无符号32位二进制除法器模块_14_out_5 ),
    .out_4(\无符号32位二进制除法器模块_18_out_4 ), .out_5(\无符号32位二进制除法器模块_18_out_5 ), .out_6(out_4[19]));
  \无符号32位二进制除法器模块  \u_无符号32位二进制除法器模块_19  (
    .in_1(\无符号32位二进制除法器模块_15_out_4 ), .in_2(in_2), .in_3(\无符号32位二进制除法器模块_15_out_5 ),
    .out_4(\无符号32位二进制除法器模块_19_out_4 ), .out_5(\无符号32位二进制除法器模块_19_out_5 ), .out_6(out_4[11]));
  \无符号32位二进制除法器模块  \u_无符号32位二进制除法器模块_20  (
    .in_1(\无符号32位二进制除法器模块_16_out_4 ), .in_2(in_2), .in_3(\无符号32位二进制除法器模块_16_out_5 ),
    .out_4(\无符号32位二进制除法器模块_20_out_4 ), .out_5(\无符号32位二进制除法器模块_20_out_5 ), .out_6(out_4[3]));
  \无符号32位二进制除法器模块  \u_无符号32位二进制除法器模块_21  (
    .in_1(\无符号32位二进制除法器模块_17_out_4 ), .in_2(in_2), .in_3(\无符号32位二进制除法器模块_17_out_5 ),
    .out_4(\无符号32位二进制除法器模块_21_out_4 ), .out_5(\无符号32位二进制除法器模块_21_out_5 ), .out_6(out_4[26]));
  \无符号32位二进制除法器模块  \u_无符号32位二进制除法器模块_22  (
    .in_1(\无符号32位二进制除法器模块_18_out_4 ), .in_2(in_2), .in_3(\无符号32位二进制除法器模块_18_out_5 ),
    .out_4(\无符号32位二进制除法器模块_22_out_4 ), .out_5(\无符号32位二进制除法器模块_22_out_5 ), .out_6(out_4[18]));
  \无符号32位二进制除法器模块  \u_无符号32位二进制除法器模块_23  (
    .in_1(\无符号32位二进制除法器模块_19_out_4 ), .in_2(in_2), .in_3(\无符号32位二进制除法器模块_19_out_5 ),
    .out_4(\无符号32位二进制除法器模块_23_out_4 ), .out_5(\无符号32位二进制除法器模块_23_out_5 ), .out_6(out_4[10]));
  \无符号32位二进制除法器模块  \u_无符号32位二进制除法器模块_24  (
    .in_1(\无符号32位二进制除法器模块_20_out_4 ), .in_2(in_2), .in_3(\无符号32位二进制除法器模块_20_out_5 ),
    .out_4(\无符号32位二进制除法器模块_24_out_4 ), .out_5(\无符号32位二进制除法器模块_24_out_5 ), .out_6(out_4[2]));
  \无符号32位二进制除法器模块  \u_无符号32位二进制除法器模块_25  (
    .in_1(\无符号32位二进制除法器模块_21_out_4 ), .in_2(in_2), .in_3(\无符号32位二进制除法器模块_21_out_5 ),
    .out_4(\无符号32位二进制除法器模块_25_out_4 ), .out_5(\无符号32位二进制除法器模块_25_out_5 ), .out_6(out_4[25]));
  \无符号32位二进制除法器模块  \u_无符号32位二进制除法器模块_26  (
    .in_1(\无符号32位二进制除法器模块_22_out_4 ), .in_2(in_2), .in_3(\无符号32位二进制除法器模块_22_out_5 ),
    .out_4(\无符号32位二进制除法器模块_26_out_4 ), .out_5(\无符号32位二进制除法器模块_26_out_5 ), .out_6(out_4[17]));
  \无符号32位二进制除法器模块  \u_无符号32位二进制除法器模块_27  (
    .in_1(\无符号32位二进制除法器模块_23_out_4 ), .in_2(in_2), .in_3(\无符号32位二进制除法器模块_23_out_5 ),
    .out_4(\无符号32位二进制除法器模块_27_out_4 ), .out_5(\无符号32位二进制除法器模块_27_out_5 ), .out_6(out_4[9]));
  \无符号32位二进制除法器模块  \u_无符号32位二进制除法器模块_28  (
    .in_1(\无符号32位二进制除法器模块_24_out_4 ), .in_2(in_2), .in_3(\无符号32位二进制除法器模块_24_out_5 ),
    .out_4(\无符号32位二进制除法器模块_28_out_4 ), .out_5(\无符号32位二进制除法器模块_28_out_5 ), .out_6(out_4[1]));
  \无符号32位二进制除法器模块  \u_无符号32位二进制除法器模块_29  (
    .in_1(\无符号32位二进制除法器模块_25_out_4 ), .in_2(in_2), .in_3(\无符号32位二进制除法器模块_25_out_5 ),
    .out_4(\无符号32位二进制除法器模块_29_out_4 ), .out_5(\无符号32位二进制除法器模块_29_out_5 ), .out_6(out_4[24]));
  \无符号32位二进制除法器模块  \u_无符号32位二进制除法器模块_30  (
    .in_1(\无符号32位二进制除法器模块_26_out_4 ), .in_2(in_2), .in_3(\无符号32位二进制除法器模块_26_out_5 ),
    .out_4(\无符号32位二进制除法器模块_30_out_4 ), .out_5(\无符号32位二进制除法器模块_30_out_5 ), .out_6(out_4[16]));
  \无符号32位二进制除法器模块  \u_无符号32位二进制除法器模块_31  (
    .in_1(\无符号32位二进制除法器模块_27_out_4 ), .in_2(in_2), .in_3(\无符号32位二进制除法器模块_27_out_5 ),
    .out_4(\无符号32位二进制除法器模块_31_out_4 ), .out_5(\无符号32位二进制除法器模块_31_out_5 ), .out_6(out_4[8]));
  \无符号32位二进制除法器模块  \u_无符号32位二进制除法器模块_32  (
    .in_1(\无符号32位二进制除法器模块_28_out_4 ), .in_2(in_2), .in_3(\无符号32位二进制除法器模块_28_out_5 ), .out_5(out_3),
    .out_6(out_4[0]));  // open: out_4
endmodule

module \无符号32位除法器封装  (
  input  [31:0] in_1,
  input  [31:0] in_2,
  output [31:0] out_3,
  output [31:0] out_4
);

  \无符号32位除法器  \u_无符号32位除法器_1  (.in_1(in_1), .in_2(in_2), .out_3(out_4), .out_4(out_3));

  // Notes on the sheet:
  //   n1(31:0)
  //   d(31:0)
  //   quot(31:0)
  //   rem(31:0)
endmodule
