// Logisim project My4.circ as structural Verilog
module \计算X_X模块SqrX  (
  input  [31:0] a,
  input  [31:0] b,
  input  [31:0] c,
  input  [31:0] d,
  output [31:0] a_prime,
  output [31:0] b_prime,
  output [31:0] c_prime,
  output [31:0] d_prime
);

  wire [31:0] multiplier_1_out, multiplier_2_out, multiplier_3_out, multiplier_4_out, multiplier_5_out,
       multiplier_6_out, multiplier_7_out;

  Multiplier #(.width(32)) multiplier_1 (.a(a), .b(a), .out(multiplier_1_out), .cin({32{1'b0}}));  // open: cout
  Multiplier #(.width(32)) multiplier_2 (.a(b), .b(c), .out(multiplier_2_out), .cin({32{1'b0}}));  // open: cout
  Multiplier #(.width(32)) multiplier_3 (.a(a), .b(b), .out(multiplier_3_out), .cin({32{1'b0}}));  // open: cout
  Multiplier #(.width(32)) multiplier_4 (.a(b), .b(d), .out(multiplier_4_out), .cin({32{1'b0}}));  // open: cout
  Multiplier #(.width(32)) multiplier_5 (.a(a), .b(c), .out(multiplier_5_out), .cin({32{1'b0}}));  // open: cout
  Multiplier #(.width(32)) multiplier_6 (.a(c), .b(d), .out(multiplier_6_out), .cin({32{1'b0}}));  // open: cout
  Multiplier #(.width(32)) multiplier_7 (.a(d), .b(d), .out(multiplier_7_out), .cin({32{1'b0}}));  // open: cout
  Adder #(.width(32)) adder_1 (.a(multiplier_1_out), .b(multiplier_2_out), .out(a_prime), .cin(1'b0));  // open: cout
  Adder #(.width(32)) adder_2 (.a(multiplier_3_out), .b(multiplier_4_out), .out(b_prime), .cin(1'b0));  // open: cout
  Adder #(.width(32)) adder_3 (.a(multiplier_5_out), .b(multiplier_6_out), .out(c_prime), .cin(1'b0));  // open: cout
  Adder #(.width(32)) adder_4 (.a(multiplier_2_out), .b(multiplier_7_out), .out(d_prime), .cin(1'b0));  // open: cout

  // Notes on the sheet:
  //   a*a
  //   b*c
  //   a*b
  //   b*d
  //   a*c
  //   c*d
  //   d*d
endmodule

module \X_X测试  (
  input  [31:0] a,
  input  [31:0] b,
  input  [31:0] c,
  input  [31:0] d,
  output [31:0] a_prime,
  output [31:0] b_prime,
  output [31:0] c_prime,
  output [31:0] d_prime
);

  \计算X_X模块SqrX  \u_计算x_x模块sqrx_1  (
    .a(a), .b(b), .c(c), .d(d), .a_prime(a_prime), .b_prime(b_prime), .c_prime(c_prime), .d_prime(d_prime));
endmodule

module \计算X_X_A模块SqrX_A  (
  input  [31:0] a,
  input  [31:0] b,
  input  [31:0] c,
  input  [31:0] d,
  output [31:0] a_prime_prime,
  output [31:0] b_prime_prime,
  output [31:0] c_prime_prime,
  output [31:0] d_prime_prime
);

  wire [31:0] adder_1_out, adder_2_out, adder_3_out, adder_4_out, multiplier_1_out, multiplier_2_out,
       multiplier_3_out, multiplier_4_out, multiplier_5_out, multiplier_6_out, multiplier_7_out;

  Multiplier #(.width(32)) multiplier_1 (.a(a), .b(b), .out(multiplier_1_out), .cin({32{1'b0}}));  // open: cout
  Multiplier #(.width(32)) multiplier_2 (.a(b), .b(d), .out(multiplier_2_out), .cin({32{1'b0}}));  // open: cout
  Multiplier #(.width(32)) multiplier_3 (.a(a), .b(a), .out(multiplier_3_out), .cin({32{1'b0}}));  // open: cout
  Multiplier #(.width(32)) multiplier_4 (.a(b), .b(c), .out(multiplier_4_out), .cin({32{1'b0}}));  // open: cout
  Multiplier #(.width(32)) multiplier_5 (.a(d), .b(d), .out(multiplier_5_out), .cin({32{1'b0}}));  // open: cout
  Multiplier #(.width(32)) multiplier_6 (.a(c), .b(a), .out(multiplier_6_out), .cin({32{1'b0}}));  // open: cout
  Multiplier #(.width(32)) multiplier_7 (.a(d), .b(c), .out(multiplier_7_out), .cin({32{1'b0}}));  // open: cout
  Adder #(.width(32)) adder_1 (
    .a(multiplier_3_out), .b(multiplier_4_out), .out(adder_1_out), .cin(1'b0));  // open: cout
  Adder #(.width(32)) adder_2 (
    .a(multiplier_1_out), .b(multiplier_2_out), .out(adder_2_out), .cin(1'b0));  // open: cout
  Adder #(.width(32)) adder_3 (
    .a(multiplier_6_out), .b(multiplier_7_out), .out(adder_3_out), .cin(1'b0));  // open: cout
  Adder #(.width(32)) adder_4 (
    .a(multiplier_5_out), .b(multiplier_4_out), .out(adder_4_out), .cin(1'b0));  // open: cout
  Adder #(.width(32)) adder_5 (
    .a(multiplier_1_out), .b(multiplier_2_out), .out(a_prime_prime), .cin(1'b0));  // open: cout
  Adder #(.width(32)) adder_6 (.a(adder_1_out), .b(adder_2_out), .out(b_prime_prime), .cin(1'b0));  // open: cout
  Adder #(.width(32)) adder_7 (
    .a(multiplier_4_out), .b(multiplier_5_out), .out(c_prime_prime), .cin(1'b0));  // open: cout
  Adder #(.width(32)) adder_8 (.a(adder_3_out), .b(adder_4_out), .out(d_prime_prime), .cin(1'b0));  // open: cout

  // Notes on the sheet:
  //   a*b
  //   b*d
  //   a*a
  //   b*c
  //   d*d
  //   a*c
  //   c*d
endmodule

module \X_X_A测试  (
  input  [31:0] a,
  input  [31:0] b,
  input  [31:0] c,
  input  [31:0] d,
  output [31:0] a_prime_prime,
  output [31:0] b_prime_prime,
  output [31:0] c_prime_prime,
  output [31:0] d_prime_prime
);

  \计算X_X_A模块SqrX_A  \u_计算x_x_a模块sqrx_a_1  (
    .a(a), .b(b), .c(c), .d(d), .a_prime_prime(a_prime_prime), .b_prime_prime(b_prime_prime),
    .c_prime_prime(c_prime_prime), .d_prime_prime(d_prime_prime));
endmodule

module \矩阵快速幂算法迭代模块  (
  input  ni_1,
  input  clr,
  input  clk,
  input  start,
  output [31:0] Fi
);

  wire buffer_1_out, buffer_2_out;
  wire [31:0] multiplexer_1_out, multiplexer_2_out, multiplexer_3_out, multiplexer_4_out, multiplexer_5_out,
       multiplexer_6_out, multiplexer_7_out, multiplexer_8_out, register_1_q, register_3_q, register_4_q,
       \计算x_x_a模块sqrx_a_1_a_prime_prime , \计算x_x_a模块sqrx_a_1_b_prime_prime ,
       \计算x_x_a模块sqrx_a_1_c_prime_prime , \计算x_x_a模块sqrx_a_1_d_prime_prime , \计算x_x模块sqrx_1_a_prime ,
       \计算x_x模块sqrx_1_b_prime , \计算x_x模块sqrx_1_c_prime , \计算x_x模块sqrx_1_d_prime ;

  buf buffer_1 (buffer_1_out, start);
  buf buffer_2 (buffer_2_out, buffer_1_out);
  Multiplexer #(.width(32), .enable("false")) multiplexer_1 (
    .in0({32{1'b0}}), .in1(multiplexer_5_out), .out(multiplexer_1_out), .sel(buffer_2_out));
  Multiplexer #(.width(32), .enable("false")) multiplexer_2 (
    .in0(32'h1), .in1(multiplexer_6_out), .out(multiplexer_2_out), .sel(buffer_2_out));
  Multiplexer #(.width(32), .enable("false")) multiplexer_3 (
    .in0(32'h1), .in1(multiplexer_7_out), .out(multiplexer_3_out), .sel(buffer_2_out));
  Multiplexer #(.width(32), .enable("false")) multiplexer_4 (
    .in0(32'h1), .in1(multiplexer_8_out), .out(multiplexer_4_out), .sel(buffer_2_out));
  Register #(.width(32)) register_1 (.D(multiplexer_1_out), .en(1'b1), .Q(register_1_q), .clk(clk), .clr(clr));
  Register #(.width(32)) register_2 (.D(multiplexer_2_out), .en(1'b1), .Q(Fi), .clk(clk), .clr(clr));
  Register #(.width(32)) register_3 (.D(multiplexer_3_out), .en(1'b1), .Q(register_3_q), .clk(clk), .clr(clr));
  Register #(.width(32)) register_4 (.D(multiplexer_4_out), .en(1'b1), .Q(register_4_q), .clk(clk), .clr(clr));
  // Probe on register_3_q
  \计算X_X模块SqrX  \u_计算x_x模块sqrx_1  (
    .a(register_1_q), .b(Fi), .c(register_3_q), .d(register_4_q), .a_prime(\计算x_x模块sqrx_1_a_prime ),
    .b_prime(\计算x_x模块sqrx_1_b_prime ), .c_prime(\计算x_x模块sqrx_1_c_prime ), .d_prime(\计算x_x模块sqrx_1_d_prime ));
  \计算X_X_A模块SqrX_A  \u_计算x_x_a模块sqrx_a_1  (
    .a(register_1_q), .b(Fi), .c(register_3_q), .d(register_4_q),
    .a_prime_prime(\计算x_x_a模块sqrx_a_1_a_prime_prime ), .b_prime_prime(\计算x_x_a模块sqrx_a_1_b_prime_prime ),
    .c_prime_prime(\计算x_x_a模块sqrx_a_1_c_prime_prime ), .d_prime_prime(\计算x_x_a模块sqrx_a_1_d_prime_prime ));
  Multiplexer #(.width(32), .enable("false")) multiplexer_5 (
    .in0(\计算x_x模块sqrx_1_a_prime ), .in1(\计算x_x_a模块sqrx_a_1_a_prime_prime ), .out(multiplexer_5_out),
    .sel(ni_1));
  Multiplexer #(.width(32), .enable("false")) multiplexer_6 (
    .in0(\计算x_x模块sqrx_1_b_prime ), .in1(\计算x_x_a模块sqrx_a_1_b_prime_prime ), .out(multiplexer_6_out),
    .sel(ni_1));
  Multiplexer #(.width(32), .enable("false")) multiplexer_7 (
    .in0(\计算x_x模块sqrx_1_c_prime ), .in1(\计算x_x_a模块sqrx_a_1_c_prime_prime ), .out(multiplexer_7_out),
    .sel(ni_1));
  Multiplexer #(.width(32), .enable("false")) multiplexer_8 (
    .in0(\计算x_x模块sqrx_1_d_prime ), .in1(\计算x_x_a模块sqrx_a_1_d_prime_prime ), .out(multiplexer_8_out),
    .sel(ni_1));
endmodule

module Display (
  input  [31:0] in_1,
  output [3:0] out_2,
  output [3:0] out_3,
  output [3:0] out_4,
  output [3:0] out_5,
  output [3:0] out_6,
  output [3:0] out_7,
  output [3:0] out_8,
  output [3:0] out_9,
  output [3:0] out_10,
  output [3:0] out_11
);

  wire [31:0] divider_1_rem, divider_2_rem, divider_3_rem, divider_4_rem, divider_5_rem, divider_6_rem,
       divider_7_rem, divider_8_rem, divider_9_rem;
  wire [31:4] divider_1_out, divider_2_out, divider_3_out, divider_4_out, divider_5_out, divider_6_out,
       divider_7_out, divider_8_out, divider_9_out, divider_10_out;

  Divider #(.width(32)) divider_1 (
    .a(in_1), .b(32'h3b9aca00), .out({divider_1_out, out_2}), .rem(divider_1_rem));  // open: upper
  Divider #(.width(32)) divider_2 (
    .a(divider_1_rem), .b(32'h5f5e100), .out({divider_2_out, out_3}), .rem(divider_2_rem));  // open: upper
  Divider #(.width(32)) divider_3 (
    .a(divider_2_rem), .b(32'h989680), .out({divider_3_out, out_4}), .rem(divider_3_rem));  // open: upper
  Divider #(.width(32)) divider_4 (
    .a(divider_3_rem), .b(32'hf4240), .out({divider_4_out, out_5}), .rem(divider_4_rem));  // open: upper
  Divider #(.width(32)) divider_5 (
    .a(divider_4_rem), .b(32'h186a0), .out({divider_5_out, out_6}), .rem(divider_5_rem));  // open: upper
  Divider #(.width(32)) divider_6 (
    .a(divider_5_rem), .b(32'h2710), .out({divider_6_out, out_7}), .rem(divider_6_rem));  // open: upper
  Divider #(.width(32)) divider_7 (
    .a(divider_6_rem), .b(32'h3e8), .out({divider_7_out, out_8}), .rem(divider_7_rem));  // open: upper
  Divider #(.width(32)) divider_8 (
    .a(divider_7_rem), .b(32'h64), .out({divider_8_out, out_9}), .rem(divider_8_rem));  // open: upper
  Divider #(.width(32)) divider_9 (
    .a(divider_8_rem), .b(32'ha), .out({divider_9_out, out_10}), .rem(divider_9_rem));  // open: upper
  Divider #(.width(32)) divider_10 (.a(divider_9_rem), .b(32'h1), .out({divider_10_out, out_11}));  // open: upper, rem

  // Notes on the sheet:
  //   4294967296
endmodule

module Controller (
  input  [5:0] n,
  input  clock,
  input  clear,
  output ni_1,
  output clk,
  output start,
  output clear_2
);

  wire buffer_1_out, buffer_2_out, comparator_1_lt, not_1_out, or_1_out, or_2_out;
  wire [5:1] shift_register_1_out;
  wire [7:0] counter_1_q;

  buf buffer_1 (buffer_1_out, buffer_2_out);
  buf buffer_2 (buffer_2_out, clear);
  not not_1 (not_1_out, buffer_1_out);
  or or_1 (or_1_out, clear, clock);
  Shift_Register #(.width(6), .length(6), .trigger("falling")) shift_register_1 (
    .shift(not_1_out), .in(n), .clk(or_1_out), .out({shift_register_1_out, ni_1}), .load(buffer_1_out),
    .clr(clear), .d0({{5{1'b0}}, n[0]}), .d1({{5{1'b0}}, n[1]}), .d2({{5{1'b0}}, n[2]}),
    .d3({{5{1'b0}}, n[3]}), .d4({{5{1'b0}}, n[4]}), .d5({{5{1'b0}}, n[5]}));  // open: q0, q1, q2, q3, q4, q5
  Counter #(.ongoal("stay"), .trigger("falling")) counter_1 (
    .count(1'b1), .Q(counter_1_q), .clk(clock), .clr(clear));  // open: load, D, carry
  Comparator #(.mode("unsigned")) comparator_1 (.a(counter_1_q), .b(8'h6), .lt(comparator_1_lt));  // open: gt, eq
  and and_1 (clk, comparator_1_lt, clock);
  D_Flip_Flop d_ff_1 (.clk(clock), .D(or_2_out), .Q(start), .reset(clear));  // open: Qn, preset, en
  or or_2 (or_2_out, start, ni_1);

  assign clear_2 = clear;
endmodule

module \主模块main  (
  input  [5:0] n,
  input  Clear,
  input  Clock
);

  wire controller_1_clear_2, controller_1_clk, controller_1_ni_1, controller_1_start;
  wire [3:0] display_1_out_2, display_1_out_3, display_1_out_4, display_1_out_5, display_1_out_6,
       display_1_out_7, display_1_out_8, display_1_out_9, display_1_out_10, display_1_out_11;
  wire [31:0] \矩阵快速幂算法迭代模块_1_fi ;

  Controller controller_1 (
    .n(n), .clock(Clock), .clear(Clear), .ni_1(controller_1_ni_1), .clk(controller_1_clk),
    .start(controller_1_start), .clear_2(controller_1_clear_2));
  \矩阵快速幂算法迭代模块  \u_矩阵快速幂算法迭代模块_1  (
    .ni_1(controller_1_ni_1), .clr(controller_1_clear_2), .clk(controller_1_clk), .start(controller_1_start),
    .Fi(\矩阵快速幂算法迭代模块_1_fi ));
  Display display_1 (
    .in_1(\矩阵快速幂算法迭代模块_1_fi ), .out_2(display_1_out_2), .out_3(display_1_out_3), .out_4(display_1_out_4),
    .out_5(display_1_out_5), .out_6(display_1_out_6), .out_7(display_1_out_7), .out_8(display_1_out_8),
    .out_9(display_1_out_9), .out_10(display_1_out_10), .out_11(display_1_out_11));
  Hex_Digit_Display hex_digit_display_1 (.value(display_1_out_3));  // open: dp
  Hex_Digit_Display hex_digit_display_2 (.value(display_1_out_2));  // open: dp
  Hex_Digit_Display hex_digit_display_3 (.value(display_1_out_5));  // open: dp
  Hex_Digit_Display hex_digit_display_4 (.value(display_1_out_4));  // open: dp
  Hex_Digit_Display hex_digit_display_5 (.value(display_1_out_6));  // open: dp
  Hex_Digit_Display hex_digit_display_6 (.value(display_1_out_8));  // open: dp
  Hex_Digit_Display hex_digit_display_7 (.value(display_1_out_7));  // open: dp
  Hex_Digit_Display hex_digit_display_8 (.value(display_1_out_9));  // open: dp
  Hex_Digit_Display hex_digit_display_9 (.value(display_1_out_11));  // open: dp
  Hex_Digit_Display hex_digit_display_10 (.value(display_1_out_10));  // open: dp
endmodule
